// Logisim project ARM_CPU.circ as structural Verilog
module main (
);

  wire decode_1_i, decode_1_rotate, decode_1_s, decode_1_shift, decode_1_si, nand_1_out, not_1_out, not_2_out;
  wire [1:0] decode_1_f, decode_1_sop, decode_1_st;
  wire [3:0] decode_1_aluop, decode_1_cond, decode_1_op4, decode_1_rd, decode_1_rm, decode_1_rn, decode_1_rs;
  wire [4:0] decode_1_rtim, decode_1_sim, multiplexer_1_out, regfile_1_sv;
  wire [5:0] decode_1_op6;
  wire [7:0] decode_1_im;
  wire [11:0] decode_1_off;
  wire [31:0] fd_1_inst0, fetch_1_inst, PC_q, pcincr_1_pc4, regfile_1_cpsrout;

  Register #(.width(32)) PC (.en(not_1_out), .Q(PC_q));  // open: D, clk, clr
  PCincr pcincr_1 (.PC(PC_q), .PC4(pcincr_1_pc4));
  Fetch fetch_1 (.Inst(fetch_1_inst));  // open: Addr
  not not_1 (not_1_out, nand_1_out);
  FD fd_1 (.Inst0(fd_1_inst0), .Inst(fetch_1_inst), .PC(pcincr_1_pc4));  // open: CLK, WE, PC0
  // NAND_Gate nand_1 has open pins: out=nand_1_out
  RegFile regfile_1 (
    .cpsrOut(regfile_1_cpsrout), .rN(decode_1_rn), .WE(nand_1_out), .rM(decode_1_rm), .SV(regfile_1_sv),
    .rS(decode_1_rs));  // open: S, W, rW, cpsrIn, Clk, M, N
  csprFlagDecode csprflagdecode_1 (.Cond(decode_1_cond), .Cspr(regfile_1_cpsrout));  // open: Execute
  Multiplexer #(.width(5), .enable("false")) multiplexer_1 (
    .in0(regfile_1_sv), .in1(decode_1_sim), .out(multiplexer_1_out), .sel(not_2_out));
  not not_2 (not_2_out, decode_1_si);
  Multiplexer #(.width(5), .enable("false")) multiplexer_2 (
    .in0(multiplexer_1_out), .in1(decode_1_rtim), .sel(decode_1_rotate));  // open: out
  Decode decode_1 (
    .rS(decode_1_rs), .SI(decode_1_si), .ST(decode_1_st), .Op6(decode_1_op6), .rD(decode_1_rd),
    .SIm(decode_1_sim), .Inst(fd_1_inst0), .rN(decode_1_rn), .S(decode_1_s), .Cond(decode_1_cond),
    .I(decode_1_i), .F(decode_1_f), .Op4(decode_1_op4), .rM(decode_1_rm), .Off(decode_1_off),
    .RtIm(decode_1_rtim), .Im(decode_1_im), .SOp(decode_1_sop), .ALUOp(decode_1_aluop),
    .Shift(decode_1_shift), .Rotate(decode_1_rotate));  // open: RSB, Carry, CMP, MOV, MOVN, BIC
  // OR_Gate or_1 has open pins: in0=decode_1_rotate, in1=decode_1_shift, out=open
endmodule

module Fetch (
  input  [23:0] Addr,
  output [31:0] Inst
);

  ROM #(.addrWidth(24), .dataWidth(32)) ROMforNow (.addr(Addr), .data(Inst));
endmodule

module FD (
  input  [31:0] Inst,
  input  [31:0] PC,
  input  WE,
  input  CLK,
  output [31:0] Inst0,
  output [31:0] PC0
);

  Register #(.width(32)) register_1 (.D(Inst), .en(WE), .clk(CLK), .Q(Inst0));  // open: clr
  Register #(.width(32)) register_2 (.D(PC), .en(WE), .clk(CLK), .Q(PC0));  // open: clr
endmodule

module Decode (
  input  [31:0] Inst,
  output [4:0] RtIm,
  output [3:0] Cond,
  output [1:0] F,
  output I,
  output [3:0] Op4,
  output S,
  output [5:0] Op6,
  output [3:0] rN,
  output [3:0] rD,
  output [3:0] rS,
  output [4:0] SIm,
  output [1:0] ST,
  output SI,
  output [3:0] rM,
  output [11:0] Off,
  output [7:0] Im,
  output Rotate,
  output [1:0] SOp,
  output Shift,
  output [3:0] ALUOp,
  output RSB,
  output Carry,
  output CMP,
  output MOV,
  output BIC,
  output MOVN
);

  wire and_1_out, and_3_out, and_4_out, and_5_out, decoder_1_out0, decoder_1_out1, decoder_1_out2,
       decoder_1_out3, decoder_1_out4, decoder_1_out5, decoder_1_out7, decoder_1_out8, decoder_1_out9,
       decoder_1_out10, decoder_1_out11;
  wire [1:0] and_6_out, and_7_out, bit_extender_1_out, bit_extender_2_out;
  wire [3:0] and_8_out, and_9_out, and_10_out, and_11_out, and_12_out, and_13_out, and_14_out, and_15_out,
       and_16_out, bit_extender_3_out, bit_extender_4_out, bit_extender_5_out, bit_extender_6_out,
       bit_extender_7_out, bit_extender_8_out, bit_extender_9_out, bit_extender_10_out, bit_extender_11_out,
       not_1_out, not_4_out;
  wire [3:1] decoder_1_out6, not_11_out, not_13_out, not_15_out, not_17_out, or_4_out;
  wire [3:2] or_1_out;

  Decoder #(.select(4), .enable("false")) decoder_1 (
    .out0(decoder_1_out0), .out1(decoder_1_out1), .out2(decoder_1_out2), .out3(decoder_1_out3),
    .out4(decoder_1_out4), .out5(decoder_1_out5), .out6(decoder_1_out6[1]), .out7(decoder_1_out7),
    .out8(decoder_1_out8), .out9(decoder_1_out9), .out10(decoder_1_out10), .out11(decoder_1_out11),
    .out12(not_11_out[2]), .out13(MOV), .out14(BIC), .out15(MOVN), .sel(Inst[24:21]));
  or or_1 (or_1_out[2], decoder_1_out2, decoder_1_out10, decoder_1_out3);
  and and_1 (and_1_out, ~Inst[27], ~Inst[26], Inst[25]);  // AND_Gate
  and and_2 (Rotate, and_1_out, ~and_3_out);  // AND_Gate
  and and_3 (and_3_out, ~Inst[27], ~Inst[26], Inst[25], Inst[24], ~Inst[22], ~Inst[21], ~Inst[20]);  // AND_Gate
  and and_4 (and_4_out, ~Inst[27], ~Inst[26], ~Inst[25]);  // AND_Gate
  and and_5 (and_5_out, ~Inst[27], Inst[26], Inst[25]);  // AND_Gate
  or or_2 (not_1_out[3], decoder_1_out0, decoder_1_out8);
  or or_3 (not_4_out[3], decoder_1_out1, decoder_1_out9);
  or or_4 (or_4_out[1], decoder_1_out4, decoder_1_out11, decoder_1_out5);
  assign bit_extender_1_out = {{1{Rotate}}, Rotate};  // Bit_Extender bit_extender_1
  assign bit_extender_2_out = {{1{Shift}}, Shift};  // Bit_Extender bit_extender_2
  or or_5 (Shift, and_4_out, and_5_out);
  assign bit_extender_3_out = {{3{not_1_out[3]}}, not_1_out[3]};  // Bit_Extender bit_extender_3
  not not_1 (not_1_out[0], not_1_out[3]);
  not not_2 (not_1_out[1], not_1_out[3]);
  not not_3 (not_1_out[2], not_1_out[3]);
  assign bit_extender_4_out = {{3{not_4_out[3]}}, not_4_out[3]};  // Bit_Extender bit_extender_4
  not not_4 (not_4_out[0], not_4_out[3]);
  not not_5 (not_4_out[1], not_4_out[3]);
  assign bit_extender_5_out = {{3{or_1_out[2]}}, or_1_out[2]};  // Bit_Extender bit_extender_5
  not not_6 (or_1_out[3], or_1_out[2]);
  assign bit_extender_6_out = {{3{or_4_out[1]}}, or_4_out[1]};  // Bit_Extender bit_extender_6
  not not_7 (or_4_out[2], or_4_out[1]);
  not not_8 (or_4_out[3], or_4_out[1]);
  assign bit_extender_7_out = {{3{decoder_1_out6[1]}}, decoder_1_out6[1]};  // Bit_Extender bit_extender_7
  not not_9 (decoder_1_out6[2], decoder_1_out6[1]);
  not not_10 (decoder_1_out6[3], decoder_1_out6[1]);
  assign bit_extender_8_out = {{3{not_11_out[2]}}, not_11_out[2]};  // Bit_Extender bit_extender_8
  not not_11 (not_11_out[1], not_11_out[2]);
  not not_12 (not_11_out[3], not_11_out[2]);
  assign bit_extender_9_out = {{3{not_13_out[2]}}, not_13_out[2]};  // Bit_Extender bit_extender_9
  not not_13 (not_13_out[1], not_13_out[2]);
  not not_14 (not_13_out[3], not_13_out[2]);
  assign bit_extender_10_out = {{3{not_15_out[2]}}, not_15_out[2]};  // Bit_Extender bit_extender_10
  not not_15 (not_15_out[1], not_15_out[2]);
  not not_16 (not_15_out[3], not_15_out[2]);
  assign bit_extender_11_out = {{3{not_17_out[2]}}, not_17_out[2]};  // Bit_Extender bit_extender_11
  not not_17 (not_17_out[1], not_17_out[2]);
  not not_18 (not_17_out[3], not_17_out[2]);
  not not_19 (RtIm[0], Inst[25]);
  assign and_6_out = bit_extender_1_out & {2{Rotate}};  // AND_Gate and_6, 2 bits wide
  assign and_7_out = Inst[6:5] & bit_extender_2_out;  // AND_Gate and_7, 2 bits wide
  assign and_8_out = bit_extender_3_out & not_1_out;  // AND_Gate and_8, 4 bits wide
  assign and_9_out = bit_extender_4_out & {{2{not_4_out[3]}}, not_4_out[1:0]};  // AND_Gate and_9, 4 bits wide
  assign and_10_out = bit_extender_5_out & {or_1_out, {2{or_1_out[2]}}};  // AND_Gate and_10, 4 bits wide
  assign and_11_out = bit_extender_6_out & {or_4_out, or_4_out[1]};  // AND_Gate and_11, 4 bits wide
  assign and_12_out = bit_extender_7_out & {decoder_1_out6, decoder_1_out6[1]};  // AND_Gate and_12, 4 bits wide
  assign and_13_out = bit_extender_8_out & {not_11_out, not_11_out[2]};  // AND_Gate and_13, 4 bits wide
  assign and_14_out = bit_extender_9_out & {not_13_out, not_13_out[2]};  // AND_Gate and_14, 4 bits wide
  assign and_15_out = bit_extender_10_out & {not_15_out, not_15_out[2]};  // AND_Gate and_15, 4 bits wide
  assign and_16_out = bit_extender_11_out & {not_17_out, not_17_out[2]};  // AND_Gate and_16, 4 bits wide
  or or_6 (RSB, decoder_1_out3, decoder_1_out7);
  or or_7 (Carry, decoder_1_out5, decoder_1_out6[1], decoder_1_out7);
  or or_8 (CMP, decoder_1_out8, decoder_1_out9, decoder_1_out10, decoder_1_out11);
  assign SOp = and_6_out | and_7_out;  // OR_Gate or_9, 2 bits wide
  assign ALUOp = and_8_out | and_9_out | and_10_out | and_11_out | and_12_out | and_13_out;  // OR_Gate or_10, 4 bits wide

  assign Cond = Inst[31:28];
  assign F = Inst[27:26];
  assign I = Inst[25];
  assign Im = Inst[7:0];
  assign Off = Inst[11:0];
  assign Op4 = Inst[24:21];
  assign Op6 = Inst[25:20];
  assign rD = Inst[15:12];
  assign rM = Inst[3:0];
  assign rN = Inst[19:16];
  assign rS = Inst[11:8];
  assign RtIm[4:1] = Inst[11:8];
  assign S = Inst[20];
  assign SI = Inst[4];
  assign SIm = Inst[11:7];
  assign ST = Inst[6:5];

  // Other names for the same wires on the sheet: CondDT[3:0] = Inst[31:28]; DestReg[3:0] = Inst[15:12];
  //   Format[1:0] = Inst[27:26]; InputReg[3:0] = Inst[19:16]; SCF = Inst[20]; OpCode[3:0] = Inst[24:21];
  //   Operand2[11:0] = Inst[11:0]; SOp_t[1:0] = Inst[6:5]

  // Notes on the sheet:
  //   operand 2
  //   rd
  //   rn
  //   set cond flags
  //   op code
  //   immediate
  //   format
  //   conditional
  //   Data Transfer
  //   Specify Other codes for operations not done by ALU
endmodule

module RegFile (
  input  [31:0] cpsrIn,
  input  S,
  input  [31:0] W,
  input  WE,
  input  Clk,
  input  [3:0] rM,
  input  [3:0] rW,
  input  [3:0] rN,
  input  [3:0] rS,
  output [31:0] cpsrOut,
  output [31:0] M,
  output [31:0] N,
  output [4:0] SV
);

  wire and_1_out, and_2_out, and_3_out, and_4_out, and_5_out, and_6_out, and_7_out, and_8_out, and_9_out,
       and_10_out, and_11_out, and_12_out, and_13_out, and_14_out, and_15_out, r0, r1, r2, r3, r4, r5, r6,
       r7, r8, r9, r10, r11, r12, r13, r14;
  wire [31:0] a1, a2, a3, a4, ip, lr, sp, v1, v2, v3, v4, v5, v6, v7, v8;
  wire [31:5] multiplexer_3_out;

  Decoder #(.select(4), .enable("false")) decoder_1 (
    .out0(r0), .out1(r1), .out2(r2), .out3(r3), .out4(r4), .out5(r5), .out6(r6), .out7(r7), .out8(r8),
    .out9(r9), .out10(r10), .out11(r11), .out12(r12), .out13(r13), .out14(r14), .sel(rW));  // open: out15
  Register #(.width(32)) cpsr (.D(cpsrIn), .en(S), .clk(Clk), .Q(cpsrOut));  // open: clr
  Register #(.width(32)) u_a1 (.D(W), .en(and_1_out), .clk(Clk), .Q(a1));  // open: clr
  and and_1 (and_1_out, WE, r0);
  Register #(.width(32)) u_a2 (.D(W), .en(and_2_out), .clk(Clk), .Q(a2));  // open: clr
  and and_2 (and_2_out, WE, r1);
  Register #(.width(32)) u_a3 (.D(W), .en(and_3_out), .clk(Clk), .Q(a3));  // open: clr
  and and_3 (and_3_out, WE, r2);
  Register #(.width(32)) u_a4 (.D(W), .en(and_4_out), .clk(Clk), .Q(a4));  // open: clr
  and and_4 (and_4_out, WE, r3);
  Register #(.width(32)) u_v1 (.D(W), .en(and_5_out), .clk(Clk), .Q(v1));  // open: clr
  and and_5 (and_5_out, WE, r4);
  Register #(.width(32)) u_v2 (.D(W), .en(and_6_out), .clk(Clk), .Q(v2));  // open: clr
  and and_6 (and_6_out, WE, r5);
  Register #(.width(32)) u_v3 (.D(W), .en(and_7_out), .clk(Clk), .Q(v3));  // open: clr
  and and_7 (and_7_out, WE, r6);
  Register #(.width(32)) u_v4 (.D(W), .en(and_8_out), .clk(Clk), .Q(v4));  // open: clr
  and and_8 (and_8_out, WE, r7);
  Register #(.width(32)) u_v5 (.D(W), .en(and_9_out), .clk(Clk), .Q(v5));  // open: clr
  and and_9 (and_9_out, WE, r8);
  Register #(.width(32)) u_v6 (.D(W), .en(and_10_out), .clk(Clk), .Q(v6));  // open: clr
  and and_10 (and_10_out, WE, r9);
  Register #(.width(32)) u_v7 (.D(W), .en(and_11_out), .clk(Clk), .Q(v7));  // open: clr
  and and_11 (and_11_out, WE, r10);
  Register #(.width(32)) u_v8 (.D(W), .en(and_12_out), .clk(Clk), .Q(v8));  // open: clr
  and and_12 (and_12_out, WE, r11);
  Register #(.width(32)) u_ip (.D(W), .en(and_13_out), .clk(Clk), .Q(ip));  // open: clr
  and and_13 (and_13_out, WE, r12);
  Register #(.width(32)) u_sp (.D(W), .en(and_14_out), .clk(Clk), .Q(sp));  // open: clr
  and and_14 (and_14_out, WE, r13);
  Register #(.width(32)) u_lr (.D(W), .en(and_15_out), .clk(Clk), .Q(lr));  // open: clr
  and and_15 (and_15_out, WE, r14);
  Multiplexer #(.select(4), .width(32), .enable("false")) multiplexer_1 (
    .in0(a1), .in1(a2), .in2(a3), .in3(a4), .in4(v1), .in5(v2), .in6(v3), .in7(v4), .in8(v5), .in9(v6),
    .in10(v7), .in11(v8), .in12(ip), .in13(sp), .in14(lr), .out(M), .sel(rM));  // open: in15
  Multiplexer #(.select(4), .width(32), .enable("false")) multiplexer_2 (
    .in0(a1), .in1(a2), .in2(a3), .in3(a4), .in4(v1), .in5(v2), .in6(v3), .in7(v4), .in8(v5), .in9(v6),
    .in10(v7), .in11(v8), .in12(ip), .in13(sp), .in14(lr), .out(N), .sel(rN));  // open: in15
  Multiplexer #(.select(4), .width(32), .enable("false")) multiplexer_3 (
    .in0(a1), .in1(a2), .in2(a3), .in3(a4), .in4(v1), .in5(v2), .in6(v3), .in7(v4), .in8(v5), .in9(v6),
    .in10(v7), .in11(v8), .in12(ip), .in13(sp), .in14(lr), .out({multiplexer_3_out, SV}), .sel(rS));  // open: in15
endmodule

module csprFlagDecode (
  input  [31:0] Cspr,
  input  [3:0] Cond,
  output Execute
);

  wire AL, and_1_out, and_2_out, and_3_out, and_4_out, and_5_out, and_6_out, and_7_out, and_8_out, and_9_out,
       and_10_out, and_11_out, and_12_out, and_13_out, and_14_out, EQ, GE, GT, HI, HS, LE, LO, LS, LT, MI,
       NE, NV, or_1_out, or_2_out, or_3_out, or_4_out, or_5_out, or_6_out, or_7_out, or_8_out, or_9_out,
       or_10_out, or_11_out, or_12_out, or_13_out, PL, VC, VS;

  Decoder #(.select(4), .enable("false")) decoder_1 (
    .out0(EQ), .out1(NE), .out2(HS), .out3(LO), .out4(MI), .out5(PL), .out6(VS), .out7(VC), .out8(HI),
    .out9(LS), .out10(GE), .out11(LT), .out12(GT), .out13(LE), .out14(AL), .out15(NV), .sel(Cond));
  and and_1 (and_1_out, EQ, Cspr[30]);
  and and_2 (and_2_out, NE, ~Cspr[30]);  // AND_Gate
  and and_3 (and_3_out, HS, Cspr[29]);
  and and_4 (and_4_out, LO, ~Cspr[29]);  // AND_Gate
  and and_5 (and_5_out, MI, Cspr[31]);
  and and_6 (and_6_out, PL, ~Cspr[31]);  // AND_Gate
  and and_7 (and_7_out, VS, Cspr[28]);
  and and_8 (and_8_out, VC, ~Cspr[28]);  // AND_Gate
  and and_9 (and_9_out, HI, Cspr[29], ~Cspr[30]);  // AND_Gate
  or or_1 (or_1_out, ~Cspr[29], Cspr[30]);  // OR_Gate
  or or_2 (or_2_out, Cspr[28], Cspr[31]);
  or or_3 (or_3_out, ~Cspr[28], ~Cspr[31]);  // OR_Gate
  or or_4 (or_4_out, ~Cspr[28], Cspr[31]);  // OR_Gate
  or or_5 (or_5_out, Cspr[28], ~Cspr[31]);  // OR_Gate
  or or_6 (or_6_out, Cspr[28], ~Cspr[30], Cspr[31]);  // OR_Gate
  or or_7 (or_7_out, ~Cspr[28], ~Cspr[30], ~Cspr[31]);  // OR_Gate
  or or_8 (or_8_out, ~Cspr[28], Cspr[30], Cspr[31]);  // OR_Gate
  or or_9 (or_9_out, Cspr[28], Cspr[30], ~Cspr[31]);  // OR_Gate
  and and_10 (and_10_out, or_1_out, LS);
  or or_10 (or_10_out, or_2_out, or_3_out);
  or or_11 (or_11_out, or_4_out, or_5_out);
  or or_12 (or_12_out, or_6_out, or_7_out);
  or or_13 (or_13_out, or_8_out, or_9_out);
  and and_11 (and_11_out, or_10_out, GE);
  and and_12 (and_12_out, or_11_out, LT);
  and and_13 (and_13_out, or_12_out, GT);
  and and_14 (and_14_out, or_13_out, LE);
  or or_14 (Execute, and_1_out, and_2_out, and_3_out, and_4_out, and_5_out, and_6_out, and_7_out, and_8_out, and_9_out, and_10_out, and_11_out, and_12_out, and_13_out, and_14_out, AL);

  // Other names for the same wires on the sheet: b0 = Cspr[28]; b1 = Cspr[29]; b2 = Cspr[30]; b3 = Cspr[31]
endmodule

module DE (
  input  [31:0] Rn,
  input  [31:0] Rm,
  input  [31:0] Rd,
  input  [31:0] Imm,
  input  I,
  input  [31:0] PC,
  input  [31:0] ALUOp,
  input  WE,
  input  CLK,
  output [31:0] N,
  output [31:0] M,
  output [31:0] D,
  output [31:0] Imm0,
  output I0,
  output [31:0] out_15,
  output [31:0] ALUOp0
);

  Register #(.width(32)) register_1 (.D(Rn), .en(WE), .clk(CLK), .Q(N));  // open: clr
  Register #(.width(32)) register_2 (.D(Rm), .en(WE), .clk(CLK), .Q(M));  // open: clr
  Register #(.width(32)) register_3 (.D(Rd), .en(WE), .clk(CLK), .Q(D));  // open: clr
  Register #(.width(32)) register_4 (.D(Imm), .en(WE), .clk(CLK), .Q(Imm0));  // open: clr
  Register #(.width(1)) register_5 (.D(I), .en(WE), .clk(CLK), .Q(I0));  // open: clr
  Register #(.width(32)) register_6 (.D(PC), .en(WE), .clk(CLK), .Q(out_15));  // open: clr
  Register #(.width(32)) register_7 (.D(ALUOp), .en(WE), .clk(CLK), .Q(ALUOp0));  // open: clr

  // Notes on the sheet:
  //   0 extend the immediate
endmodule

module Execute (
  input  [31:0] WbN,
  input  [31:0] MemN,
  input  [31:0] N,
  input  [31:0] M,
  input  [31:0] MemM,
  input  [31:0] WbM,
  input  [3:0] ALUOp,
  input  [3:0] Rd,
  input  [1:0] ForwardM,
  input  [1:0] ForwardN,
  input  [1:0] ShiftOp,
  input  [4:0] SA,
  output [31:0] C
);

  wire [31:0] mux3x1_1_a0, shift_1_mn;

  Mux3x1 mux3x1_1 (.SWBEX(ForwardM[1]), .A(M), .SMEX(ForwardM[0]), .MemA(MemM), .WBA(WbM), .A0(mux3x1_1_a0));
  Shift shift_1 (.M(mux3x1_1_a0), .S(SA), .SOp(ShiftOp), .Mn(shift_1_mn));
  ALU alu_1 (.WBN(WbN), .MemN(MemN), .N(N), .ForwardN(ForwardN), .M(shift_1_mn), .ALUop(ALUOp), .C(C));
endmodule

module ALU (
  input  [31:0] WBN,
  input  [31:0] MemN,
  input  [31:0] N,
  input  [1:0] ForwardN,
  input  [31:0] M,
  input  [3:0] ALUop,
  output [31:0] C
);

  wire [31:0] mux3x1_1_a0;

  Mux3x1 mux3x1_1 (.SWBEX(ForwardN[1]), .A(N), .SMEX(ForwardN[0]), .MemA(MemN), .WBA(WBN), .A0(mux3x1_1_a0));
  // ARM_ALU arm_alu_1: pin names not known; wires that end beside it: mux3x1_1_a0, M, ALUop, {5{1'b0}}, 2'b00, C
endmodule

module HB (
  input  [4:0] ExMemRd,
  input  [4:0] IdExRa,
  input  [4:0] IdExRb,
  input  [4:0] MemWbRd,
  input  Im0,
  input  EnablM,
  input  MovM,
  input  EnblW,
  input  MovW,
  output out_10,
  output out_11,
  output out_12,
  output out_13
);

  wire and_1_out, and_2_out, and_3_out, and_4_out, and_5_out, and_6_out, and_7_out, and_8_out, and_9_out,
       and_10_out, eq_1_eq, eq_2_eq, eq_3_eq, eq_4_eq, nand_1_out, nand_2_out, or_1_out, or_2_out;

  or or_1 (or_1_out, ExMemRd[0], ExMemRd[1], ExMemRd[2], ExMemRd[3], ExMemRd[4]);
  EQ eq_1 (.A(ExMemRd), .B(IdExRa), .EQ(eq_1_eq));
  EQ eq_2 (.A(ExMemRd), .B(IdExRb), .EQ(eq_2_eq));
  or or_2 (or_2_out, MemWbRd[0], MemWbRd[1], MemWbRd[2], MemWbRd[3], MemWbRd[4]);
  EQ eq_3 (.A(MemWbRd), .B(IdExRa), .EQ(eq_3_eq));
  EQ eq_4 (.A(MemWbRd), .B(IdExRb), .EQ(eq_4_eq));
  and and_1 (and_1_out, or_1_out, eq_1_eq);
  and and_2 (and_2_out, or_1_out, eq_2_eq);
  nand nand_1 (nand_1_out, or_1_out, eq_1_eq);
  and and_3 (and_3_out, nand_1_out, or_2_out, eq_3_eq);
  nand nand_2 (nand_2_out, or_1_out, eq_2_eq);
  and and_4 (and_4_out, nand_2_out, or_2_out, eq_4_eq);
  and and_5 (and_5_out, and_2_out, ~Im0);  // AND_Gate
  and and_6 (and_6_out, ~Im0, and_4_out);  // AND_Gate
  and and_7 (and_7_out, and_1_out, MovM);
  and and_8 (and_8_out, and_5_out, MovM);
  and and_9 (and_9_out, and_3_out, MovW);
  and and_10 (and_10_out, and_6_out, MovW);
  Multiplexer #(.enable("false")) multiplexer_1 (.in0(and_1_out), .in1(and_7_out), .out(out_10), .sel(EnablM));
  Multiplexer #(.enable("false")) multiplexer_2 (.in0(and_5_out), .in1(and_8_out), .out(out_11), .sel(EnablM));
  Multiplexer #(.enable("false")) multiplexer_3 (.in0(and_3_out), .in1(and_9_out), .out(out_12), .sel(EnblW));
  Multiplexer #(.enable("false")) multiplexer_4 (.in0(and_6_out), .in1(and_10_out), .out(out_13), .sel(EnblW));
endmodule

module Shift (
  input  [31:0] M,
  input  [4:0] S,
  input  [1:0] SOp,
  output [31:0] Mn
);

  wire and_1_out, and_2_out, multiplexer_1_out, or_1_out, or_2_out, xor_1_out;
  wire [31:0] ls_1_mn, multiplexer_2_out, switch_1_mn, switch_2_mn;

  xor xor_1 (xor_1_out, SOp[0], SOp[0]);
  Switch switch_1 (.M(M), .Mn(switch_1_mn));
  Multiplexer #(.enable("false")) multiplexer_1 (
    .in0(xor_1_out), .in1(M[31]), .out(multiplexer_1_out), .sel(and_1_out));
  and and_1 (and_1_out, ~SOp[0], SOp[1]);  // AND_Gate
  Multiplexer #(.width(32), .enable("false")) multiplexer_2 (
    .in0(M), .in1(switch_1_mn), .out(multiplexer_2_out), .sel(or_1_out));
  or or_1 (or_1_out, SOp[0], SOp[1]);
  and and_2 (and_2_out, SOp[0], SOp[1]);
  LS ls_1 (.M(multiplexer_2_out), .S(S), .C(multiplexer_1_out), .R(and_2_out), .Mn(ls_1_mn));
  Multiplexer #(.width(32), .enable("false")) multiplexer_3 (
    .in0(ls_1_mn), .in1(switch_2_mn), .out(Mn), .sel(or_2_out));
  Switch switch_2 (.M(ls_1_mn), .Mn(switch_2_mn));
  or or_2 (or_2_out, SOp[0], SOp[1]);
endmodule

module LS (
  input  [31:0] M,
  input  [4:0] S,
  input  C,
  input  R,
  output [31:0] Mn
);

  wire [31:0] l2_1_mn, l4_1_mn, l8_1_mn, l16_1_mn;

  L16 l16_1 (.M(M), .S(S[4]), .C(C), .R(R), .Mn(l16_1_mn));
  L8 l8_1 (.M(l16_1_mn), .S(S[3]), .C(C), .R(R), .Mn(l8_1_mn));
  L4 l4_1 (.M(l8_1_mn), .S(S[2]), .C(C), .R(R), .Mn(l4_1_mn));
  L2 l2_1 (.M(l4_1_mn), .S(S[1]), .C(C), .R(R), .Mn(l2_1_mn));
  L1 l1_1 (.M(l2_1_mn), .S(S[0]), .C(C), .R(R), .Mn(Mn));
endmodule

module L1 (
  input  [31:0] M,
  input  S,
  input  C,
  input  R,
  output [31:0] Mn
);

  wire [0:0] multiplexer_1_out;

  Multiplexer #(.enable("false")) multiplexer_1 (.in0(C), .in1(M[31]), .out(multiplexer_1_out[0]), .sel(R));
  Multiplexer #(.width(32), .enable("false")) multiplexer_2 (
    .in0(M), .in1({M[30:0], multiplexer_1_out[0]}), .out(Mn), .sel(S));
endmodule

module L2 (
  input  [31:0] M,
  input  S,
  input  C,
  input  R,
  output [31:0] Mn
);

  wire [1:0] bit_extender_1_out, multiplexer_1_out;

  assign bit_extender_1_out = {{1{C}}, C};  // Bit_Extender bit_extender_1
  Multiplexer #(.width(2), .enable("false")) multiplexer_1 (
    .in0(bit_extender_1_out), .in1({M[30], M[31]}), .out(multiplexer_1_out), .sel(R));
  Multiplexer #(.width(32), .enable("false")) multiplexer_2 (
    .in0(M), .in1({M[29:0], multiplexer_1_out[0], multiplexer_1_out[1]}), .out(Mn), .sel(S));
endmodule

module L4 (
  input  [31:0] M,
  input  S,
  input  C,
  input  R,
  output [31:0] Mn
);

  wire [3:0] bit_extender_1_out, multiplexer_1_out;

  assign bit_extender_1_out = {{3{C}}, C};  // Bit_Extender bit_extender_1
  Multiplexer #(.width(4), .enable("false")) multiplexer_1 (
    .in0(bit_extender_1_out), .in1({M[28], M[29], M[30], M[31]}), .out(multiplexer_1_out), .sel(R));
  Multiplexer #(.width(32), .enable("false")) multiplexer_2 (
    .in0(M),
    .in1({M[27:0], multiplexer_1_out[0], multiplexer_1_out[1], multiplexer_1_out[2], multiplexer_1_out[3]}),
    .out(Mn), .sel(S));
endmodule

module L8 (
  input  [31:0] M,
  input  S,
  input  C,
  input  R,
  output [31:0] Mn
);

  wire [7:0] bit_extender_1_out, multiplexer_1_out;

  assign bit_extender_1_out = {{7{C}}, C};  // Bit_Extender bit_extender_1
  Multiplexer #(.width(8), .enable("false")) multiplexer_1 (
    .in0(bit_extender_1_out), .in1({M[24], M[25], M[26], M[27], M[28], M[29], M[30], M[31]}),
    .out(multiplexer_1_out), .sel(R));
  Multiplexer #(.width(32), .enable("false")) multiplexer_2 (
    .in0(M),
    .in1({M[23:0], multiplexer_1_out[0], multiplexer_1_out[1], multiplexer_1_out[2], multiplexer_1_out[3], multiplexer_1_out[4], multiplexer_1_out[5], multiplexer_1_out[6], multiplexer_1_out[7]}),
    .out(Mn), .sel(S));
endmodule

module L16 (
  input  [31:0] M,
  input  S,
  input  C,
  input  R,
  output [31:0] Mn
);

  wire [15:0] bit_extender_1_out, multiplexer_1_out;

  assign bit_extender_1_out = {{15{C}}, C};  // Bit_Extender bit_extender_1
  Multiplexer #(.width(16), .enable("false")) multiplexer_1 (
    .in0(bit_extender_1_out),
    .in1({M[16], M[17], M[18], M[19], M[20], M[21], M[22], M[23], M[24], M[25], M[26], M[27], M[28], M[29], M[30], M[31]}),
    .out(multiplexer_1_out), .sel(R));
  Multiplexer #(.width(32), .enable("false")) multiplexer_2 (
    .in0(M),
    .in1({M[15:0], multiplexer_1_out[0], multiplexer_1_out[1], multiplexer_1_out[2], multiplexer_1_out[3], multiplexer_1_out[4], multiplexer_1_out[5], multiplexer_1_out[6], multiplexer_1_out[7], multiplexer_1_out[8], multiplexer_1_out[9], multiplexer_1_out[10], multiplexer_1_out[11], multiplexer_1_out[12], multiplexer_1_out[13], multiplexer_1_out[14], multiplexer_1_out[15]}),
    .out(Mn), .sel(S));
endmodule

module Switch (
  input  [31:0] M,
  output [31:0] Mn
);


  assign Mn = {M[0], M[1], M[2], M[3], M[4], M[5], M[6], M[7], M[8], M[9], M[10], M[11], M[12], M[13], M[14], M[15], M[16], M[17], M[18], M[19], M[20], M[21], M[22], M[23], M[24], M[25], M[26], M[27], M[28], M[29], M[30], M[31]};
endmodule

module Mux3x1 (
  input  [31:0] A,
  input  [31:0] MemA,
  input  [31:0] WBA,
  input  SMEX,
  input  SWBEX,
  output [31:0] A0
);

  wire [31:0] multiplexer_1_out;

  Multiplexer #(.width(32), .enable("false")) multiplexer_1 (.in0(A), .in1(MemA), .out(multiplexer_1_out), .sel(SMEX));
  Multiplexer #(.width(32), .enable("false")) multiplexer_2 (.in0(multiplexer_1_out), .in1(WBA), .out(A0), .sel(SWBEX));
endmodule

module EQ (
  input  [4:0] A,
  input  [4:0] B,
  output EQ
);

  wire [4:0] xnor_1_out;

  assign xnor_1_out = ~(A ^ B);  // XNOR_Gate xnor_1, 5 bits wide
  and and_1 (EQ, xnor_1_out[0], xnor_1_out[1], xnor_1_out[2], xnor_1_out[3], xnor_1_out[4]);
endmodule

module PCincr (
  input  [31:0] PC,
  output [31:0] PC4
);

  // Incrementer #(.width(30)) incrementer_1: pin names not known; wires that end beside it: PC[31:2], PC4[31:2]

  assign PC4[1:0] = PC[1:0];
endmodule
