// Logisim project ARM_CPU.circ as structural Verilog
module main (
);

  wire and_1_out, Ex, I, Link, nand_1_out, undriven_2;
  wire [1:0] decode_1_shift, decode_1_sop, F;
  wire [3:0] decode_1_aluop, Rd, Rm, Rn, Rs, undriven;
  wire [4:0] decode_1_mov, regfile_1_sv, SR;
  wire [31:0] BAddr, fd_1_inst0, fd_1_pc0, fetch_1_inst, IO, multiplexer_1_out, PC_q, pcincr_1_pc4,
       regfile_1_cpsrout, regfile_1_m, regfile_1_n, undriven_3, undriven_4;

  Register #(.width(32)) PC (.D(multiplexer_1_out), .Q(PC_q));  // open: en, clk, clr
  PCincr pcincr_1 (.PC(PC_q), .PC4(pcincr_1_pc4));
  Multiplexer #(.width(32), .enable("false")) multiplexer_1 (
    .in0(BAddr), .in1(pcincr_1_pc4), .out(multiplexer_1_out), .sel(and_1_out));
  and and_1 (and_1_out, ~F[0], F[1], Ex);  // AND_Gate
  Fetch fetch_1 (.Inst(fetch_1_inst));  // open: Addr, CLK
  // NOT_Gate not_1 has open pins: in=nand_1_out, out=open
  FD fd_1 (.Inst0(fd_1_inst0), .Inst(fetch_1_inst), .PC(pcincr_1_pc4), .PC0(fd_1_pc0));  // open: WE, CLK
  // NAND_Gate nand_1 has open pins: out=nand_1_out
  Decode decode_1 (
    .Link(Link), .SRImm(SR), .SCF(decode_1_mov[4]), .Mov(decode_1_mov[0]), .Inst(fd_1_inst0),
    .Cmp(decode_1_mov[1]), .Shift(decode_1_shift[0]), .ImmOff(IO), .BAddr(BAddr), .SOp(decode_1_sop),
    .Rev(decode_1_mov[3]), .PC(fd_1_pc0), .Format(F), .CPSR(regfile_1_cpsrout), .Car(decode_1_mov[2]),
    .Rot(decode_1_shift[1]), .ALUOp(decode_1_aluop), .Execute(Ex), .Rn(Rn), .Rd(Rd), .Rm(Rm), .Rs(Rs), .I(I));  // open: MEMOp, ToAddr, SrSi
  RegFile regfile_1 (
    .M(regfile_1_m), .cpsrOut(regfile_1_cpsrout), .S(undriven_2), .cpsrIn(undriven_3), .rN(Rn), .rM(Rm),
    .rW(undriven), .N(regfile_1_n), .SV(regfile_1_sv), .rS(Rs));  // open: Clk, W, WE
  DE de_1 (
    .M(regfile_1_m), .N(regfile_1_n), .ImmOff(IO), .I(I), .CPSR(undriven_4), .ALUOp(decode_1_aluop), .Rd(Rd),
    .S(regfile_1_sv), .SRimm(decode_1_mov), .Shifts({decode_1_sop, decode_1_shift}));  // open: BAddr, COND, ALUbit, ToMem, MEMOp, WE, CLK, Mo, No, Io, Ba, I0, CPSRo, ALUOpo, Rdo, CONDo, So, SRimmo, ALUbitso, Shiftso, ToM, MOp
  Execute execute_1 ();  // open: WbN, MemN, N, M, MemM, WbM, ALUOp, Rd, ForwardM, ForwardN, ShiftOp, SA, SetCondFlag, C, COND, SCF
endmodule

module Fetch (
  input  [23:0] Addr,
  input  CLK,
  output [31:0] Inst
);

  ROM #(.addrWidth(24), .dataWidth(32)) rom_1 (.addr(Addr), .data(Inst));
endmodule

module FD (
  input  [31:0] Inst,
  input  [31:0] PC,
  input  WE,
  input  CLK,
  output [31:0] Inst0,
  output [31:0] PC0
);

  Register #(.width(32)) register_1 (.D(Inst), .en(WE), .clk(CLK), .Q(Inst0));  // open: clr
  Register #(.width(32)) register_2 (.D(PC), .en(WE), .clk(CLK), .Q(PC0));  // open: clr
endmodule

module Decode (
  input  [31:0] Inst,
  input  [31:0] CPSR,
  input  [31:0] PC,
  output Mov,
  output Cmp,
  output Car,
  output Rev,
  output SCF,
  output Shift,
  output Rot,
  output [1:0] SOp,
  output I,
  output [4:0] SRImm,
  output [31:0] ImmOff,
  output [3:0] ToAddr,
  output [1:0] MEMOp,
  output Link,
  output [31:0] BAddr,
  output [3:0] ALUOp,
  output [1:0] Format,
  output Execute,
  output [3:0] Rn,
  output [3:0] Rd,
  output [3:0] Rm,
  output [3:0] Rs,
  output SrSi
);

  wire op2decode_1_isld;
  wire [3:0] aludecode_1_aluop, memdecode_1_aluop;
  wire [31:0] bit_extender_1_out, demultiplexer_1_out0, demultiplexer_1_out1, demultiplexer_1_out2,
       op2decode_1_imm;

  Demultiplexer #(.select(2), .width(32), .enable("false")) demultiplexer_1 (
    .out0(demultiplexer_1_out0), .out1(demultiplexer_1_out1), .out2(demultiplexer_1_out2), .in(Inst),
    .sel(Inst[27:26]));  // open: out3
  OP2decode op2decode_1 (
    .Inst(Inst), .IsLd(op2decode_1_isld), .SRimm(SRImm), .Imm(op2decode_1_imm), .Rot(Rot), .SOp(SOp),
    .Shift(Shift), .Rm(Rm), .Rs(Rs), .SrSi(SrSi));
  ALUdecode aludecode_1 (
    .SetFlags(SCF), .SetFlag(demultiplexer_1_out0[20]), .Reverse(Rev), .OpCode(demultiplexer_1_out0[24:21]),
    .Carry(Car), .Move(Mov), .Compare(Cmp), .ALUOp(aludecode_1_aluop));
  MEMdecode memdecode_1 (
    .OffAddr(ToAddr[1]), .PostAddr(ToAddr[0]), .ALUOp(memdecode_1_aluop), .PreAddr(ToAddr[2]),
    .OpCode({demultiplexer_1_out1[20], demultiplexer_1_out1[21], demultiplexer_1_out1[22], demultiplexer_1_out1[23], demultiplexer_1_out1[24]}),
    .Norm(ToAddr[3]), .MEMOp(MEMOp));
  BRAdecode bradecode_1 (
    .One(demultiplexer_1_out2[25]), .LorH(demultiplexer_1_out2[24]), .Link(Link), .Baddr(Inst[23:0]),
    .Cond(Inst[31:28]), .PC(PC), .MAddr(BAddr));
  CPSRDecode cpsrdecode_1 (.Execute(Execute), .Cspr(CPSR), .Cond(Inst[31:28]));
  Multiplexer #(.select(2), .width(4), .enable("false")) multiplexer_1 (
    .in0(aludecode_1_aluop), .in1(memdecode_1_aluop), .out(ALUOp), .sel(Inst[27:26]));  // open: in2, in3
  assign bit_extender_1_out = {{20{1'b0}}, Inst[11:0]};  // Bit_Extender bit_extender_1
  Multiplexer #(.width(32), .enable("false")) multiplexer_2 (
    .in0(op2decode_1_imm), .in1(bit_extender_1_out), .out(ImmOff), .sel(op2decode_1_isld));

  assign Format = Inst[27:26];
  assign I = Inst[25];
  assign Rd = Inst[15:12];
  assign Rn = Inst[19:16];

  // Other names for the same wires on the sheet: Baddr_t[23:0] = Inst[23:0]; Op2[11:0] = Inst[11:0];
  //   C[3:0] = Inst[31:28]; F[1:0] = Inst[27:26]

  // Notes on the sheet:
  //   data proccessing 
  //   Loads and stores
  //   branches
  //   Type of Addressing Mode
endmodule

module ALUdecode (
  input  SetFlag,
  input  [3:0] OpCode,
  output Move,
  output Compare,
  output Carry,
  output Reverse,
  output SetFlags,
  output [3:0] ALUOp
);

  wire [3:0] adcs_out, adds_out, ands_out, bics_out, bit_extender_1_out, bit_extender_2_out,
       bit_extender_3_out, bit_extender_4_out, bit_extender_5_out, bit_extender_6_out, bit_extender_7_out,
       bit_extender_8_out, bit_extender_9_out, bit_extender_10_out, bit_extender_11_out, bit_extender_12_out,
       bit_extender_13_out, bit_extender_14_out, bit_extender_15_out, bit_extender_16_out, cmns_out,
       cmps_out, eors_out, movs_out, mvns_out, not_17_out, orrs_out, rsbs_out, rscs_out, sbcs_out, subs_out,
       teqs_out, tsts_out;
  wire [3:1] decoder_1_out1, not_5_out, not_7_out, not_8_out, not_9_out, not_11_out, not_13_out, not_19_out,
       not_20_out, not_22_out;
  wire [3:2] decoder_1_out0, decoder_1_out8, decoder_1_out14;
  wire [3:3] decoder_1_out13, decoder_1_out15;

  or or_1 (Move, decoder_1_out13[3], decoder_1_out15[3]);
  or or_2 (Compare, not_19_out[3], not_20_out[3]);
  or or_3 (Carry, not_11_out[3], not_13_out[3], not_9_out[3]);
  or or_4 (Reverse, not_7_out[3], not_13_out[3]);
  Decoder #(.select(4), .enable("false")) decoder_1 (
    .out0(decoder_1_out0[2]), .out1(decoder_1_out1[1]), .out2(not_5_out[3]), .out3(not_7_out[3]),
    .out4(not_8_out[3]), .out5(not_9_out[3]), .out6(not_11_out[3]), .out7(not_13_out[3]),
    .out8(decoder_1_out8[2]), .out9(not_17_out[2]), .out10(not_19_out[3]), .out11(not_20_out[3]),
    .out12(not_22_out[2]), .out13(decoder_1_out13[3]), .out14(decoder_1_out14[2]),
    .out15(decoder_1_out15[3]), .sel(OpCode));
  assign bit_extender_1_out = {{3{decoder_1_out0[2]}}, decoder_1_out0[2]};  // Bit_Extender bit_extender_1
  assign ands_out = bit_extender_1_out & ~{decoder_1_out0, {2{decoder_1_out0[2]}}};  // AND_Gate ands, 4 bits wide
  not not_1 (decoder_1_out0[3], decoder_1_out0[2]);
  assign bit_extender_2_out = {{3{decoder_1_out1[1]}}, decoder_1_out1[1]};  // Bit_Extender bit_extender_2
  assign eors_out = bit_extender_2_out & ~{decoder_1_out1, decoder_1_out1[1]};  // AND_Gate eors, 4 bits wide
  not not_2 (decoder_1_out1[3], decoder_1_out1[1]);
  not not_3 (decoder_1_out1[2], decoder_1_out1[1]);
  assign bit_extender_3_out = {{3{not_5_out[3]}}, not_5_out[3]};  // Bit_Extender bit_extender_3
  assign subs_out = bit_extender_3_out & ~{not_5_out, not_5_out[3]};  // AND_Gate subs, 4 bits wide
  not not_4 (not_5_out[2], not_5_out[3]);
  not not_5 (not_5_out[1], not_5_out[3]);
  assign bit_extender_4_out = {{3{not_7_out[3]}}, not_7_out[3]};  // Bit_Extender bit_extender_4
  assign rsbs_out = bit_extender_4_out & ~{not_7_out, not_7_out[3]};  // AND_Gate rsbs, 4 bits wide
  not not_6 (not_7_out[2], not_7_out[3]);
  not not_7 (not_7_out[1], not_7_out[3]);
  assign bit_extender_5_out = {{3{not_8_out[3]}}, not_8_out[3]};  // Bit_Extender bit_extender_5
  assign adds_out = bit_extender_5_out & ~{{2{not_8_out[3]}}, not_8_out[1], not_8_out[3]};  // AND_Gate adds, 4 bits wide
  not not_8 (not_8_out[1], not_8_out[3]);
  assign bit_extender_6_out = {{3{not_9_out[3]}}, not_9_out[3]};  // Bit_Extender bit_extender_6
  assign adcs_out = bit_extender_6_out & ~{{2{not_9_out[3]}}, not_9_out[1], not_9_out[3]};  // AND_Gate adcs, 4 bits wide
  not not_9 (not_9_out[1], not_9_out[3]);
  assign bit_extender_7_out = {{3{not_11_out[3]}}, not_11_out[3]};  // Bit_Extender bit_extender_7
  assign sbcs_out = bit_extender_7_out & ~{not_11_out, not_11_out[3]};  // AND_Gate sbcs, 4 bits wide
  not not_10 (not_11_out[2], not_11_out[3]);
  not not_11 (not_11_out[1], not_11_out[3]);
  assign bit_extender_8_out = {{3{not_13_out[3]}}, not_13_out[3]};  // Bit_Extender bit_extender_8
  assign rscs_out = bit_extender_8_out & ~{not_13_out, not_13_out[3]};  // AND_Gate rscs, 4 bits wide
  not not_12 (not_13_out[2], not_13_out[3]);
  not not_13 (not_13_out[1], not_13_out[3]);
  assign bit_extender_9_out = {{3{decoder_1_out8[2]}}, decoder_1_out8[2]};  // Bit_Extender bit_extender_9
  assign tsts_out = bit_extender_9_out & ~{decoder_1_out8, {2{decoder_1_out8[2]}}};  // AND_Gate tsts, 4 bits wide
  not not_14 (decoder_1_out8[3], decoder_1_out8[2]);
  assign bit_extender_10_out = {{3{not_17_out[2]}}, not_17_out[2]};  // Bit_Extender bit_extender_10
  assign teqs_out = bit_extender_10_out & ~not_17_out;  // AND_Gate teqs, 4 bits wide
  not not_15 (not_17_out[3], not_17_out[2]);
  not not_16 (not_17_out[1], not_17_out[2]);
  not not_17 (not_17_out[0], not_17_out[2]);
  assign bit_extender_11_out = {{3{not_19_out[3]}}, not_19_out[3]};  // Bit_Extender bit_extender_11
  assign cmps_out = bit_extender_11_out & ~{not_19_out, not_19_out[3]};  // AND_Gate cmps, 4 bits wide
  not not_18 (not_19_out[2], not_19_out[3]);
  not not_19 (not_19_out[1], not_19_out[3]);
  assign bit_extender_12_out = {{3{not_20_out[3]}}, not_20_out[3]};  // Bit_Extender bit_extender_12
  assign cmns_out = bit_extender_12_out & ~{{2{not_20_out[3]}}, not_20_out[1], not_20_out[3]};  // AND_Gate cmns, 4 bits wide
  not not_20 (not_20_out[1], not_20_out[3]);
  assign bit_extender_13_out = {{3{not_22_out[2]}}, not_22_out[2]};  // Bit_Extender bit_extender_13
  assign orrs_out = bit_extender_13_out & ~{not_22_out, not_22_out[2]};  // AND_Gate orrs, 4 bits wide
  not not_21 (not_22_out[3], not_22_out[2]);
  not not_22 (not_22_out[1], not_22_out[2]);
  assign bit_extender_14_out = {{3{decoder_1_out13[3]}}, decoder_1_out13[3]};  // Bit_Extender bit_extender_14
  assign movs_out = bit_extender_14_out & ~{4{decoder_1_out13[3]}};  // AND_Gate movs, 4 bits wide
  assign bit_extender_15_out = {{3{decoder_1_out14[2]}}, decoder_1_out14[2]};  // Bit_Extender bit_extender_15
  assign bics_out = bit_extender_15_out & ~{decoder_1_out14, {2{decoder_1_out14[2]}}};  // AND_Gate bics, 4 bits wide
  not not_23 (decoder_1_out14[3], decoder_1_out14[2]);
  assign bit_extender_16_out = {{3{decoder_1_out15[3]}}, decoder_1_out15[3]};  // Bit_Extender bit_extender_16
  assign mvns_out = bit_extender_16_out & ~{4{decoder_1_out15[3]}};  // AND_Gate mvns, 4 bits wide
  assign ALUOp = ands_out | eors_out | subs_out | rsbs_out | adds_out | adcs_out | sbcs_out | rscs_out | tsts_out | teqs_out | cmps_out | cmns_out | orrs_out | movs_out | bics_out | mvns_out;  // OR_Gate or_5, 4 bits wide

  assign SetFlags = SetFlag;

  // Notes on the sheet:
  //   Need move ops to be 0
endmodule

module MEMdecode (
  input  [4:0] OpCode,
  output PostAddr,
  output OffAddr,
  output PreAddr,
  output Norm,
  output [3:0] ALUOp,
  output [1:0] MEMOp
);

  wire [3:0] Add_out, bit_extender_1_out, bit_extender_2_out, Sub_out;
  wire [3:1] not_2_out, not_3_out;

  and and_1 (PostAddr, ~OpCode[0], OpCode[3]);  // AND_Gate
  and and_2 (OffAddr, OpCode[0], ~OpCode[3]);  // AND_Gate
  and and_3 (PreAddr, OpCode[0], OpCode[3]);
  Decoder #(.enable("false")) decoder_1 (.out0(not_2_out[3]), .out1(not_3_out[3]), .sel(OpCode[1]));
  assign bit_extender_1_out = {{3{not_2_out[3]}}, not_2_out[3]};  // Bit_Extender bit_extender_1
  assign Sub_out = bit_extender_1_out & ~{not_2_out, not_2_out[3]};  // AND_Gate Sub, 4 bits wide
  not not_1 (not_2_out[2], not_2_out[3]);
  not not_2 (not_2_out[1], not_2_out[3]);
  assign bit_extender_2_out = {{3{not_3_out[3]}}, not_3_out[3]};  // Bit_Extender bit_extender_2
  assign Add_out = bit_extender_2_out & ~{{2{not_3_out[3]}}, not_3_out[1], not_3_out[3]};  // AND_Gate Add, 4 bits wide
  not not_3 (not_3_out[1], not_3_out[3]);
  and and_4 (Norm, ~PostAddr, ~OffAddr, ~PreAddr);  // AND_Gate
  assign ALUOp = Sub_out | Add_out;  // OR_Gate or_1, 4 bits wide

  assign MEMOp = {OpCode[4], OpCode[2]};

  // Other names for the same wires on the sheet: B = OpCode[2]; L = OpCode[4]; P = OpCode[0]; U = OpCode[1];
  //   W = OpCode[3]

  // Notes on the sheet:
  //   11 -> pre-index addressing
  //   00 -> Normal Operations
  //   01 -> translation stores
  //   10 -> offset addressing
  //   00 -> SW
  //   01 -> SBU
  //   10 -> LW
  //   11 -> LBU
endmodule

module BRAdecode (
  input  [3:0] Cond,
  input  LorH,
  input  One,
  input  [23:0] Baddr,
  input  [31:0] PC,
  output Link,
  output [31:0] MAddr
);

  wire and_1_out;
  wire [1:0] not_1_out;
  wire [29:0] bit_extender_1_out;
  wire [31:0] adder_1_out;

  and and_1 (and_1_out, Cond[0], Cond[1], Cond[2], Cond[3]);
  not not_1 (not_1_out[0], One);
  assign bit_extender_1_out = {{6{Baddr[23]}}, Baddr};  // Bit_Extender bit_extender_1
  Multiplexer #(.enable("false")) multiplexer_1 (.in0(not_1_out[0]), .in1(LorH), .out(not_1_out[1]), .sel(and_1_out));
  Adder #(.width(32)) adder_1 (.a(PC), .b({bit_extender_1_out, not_1_out}), .out(adder_1_out));  // open: cin, cout
  and and_2 (Link, LorH, ~and_1_out);  // AND_Gate
  Multiplexer #(.width(32), .enable("false")) multiplexer_2 (
    .in0(adder_1_out), .in1({bit_extender_1_out, not_1_out}), .out(MAddr), .sel(and_1_out));

  // Notes on the sheet:
  //   still need to change cpsr
  //   if 1 then blx
  //   Calculating Branches in Decode
  //   0 if B, 1 if BL
endmodule

module OP2decode (
  input  [31:0] Inst,
  output IsLd,
  output [4:0] SRimm,
  output [31:0] Imm,
  output Rot,
  output [1:0] SOp,
  output Shift,
  output [3:0] Rm,
  output [3:0] Rs,
  output SrSi
);

  wire and_1_out, and_3_out, and_4_out, and_5_out;
  wire [0:0] not_1_out;
  wire [1:0] and_6_out, and_7_out, bit_extender_1_out, bit_extender_2_out;
  wire [4:0] bit_extender_3_out;

  and and_1 (and_1_out, ~Inst[27], ~Inst[26], Inst[25]);  // AND_Gate
  and and_2 (Rot, and_1_out, ~and_3_out);  // AND_Gate
  and and_3 (and_3_out, ~Inst[27], ~Inst[26], Inst[25], Inst[24], ~Inst[22], ~Inst[21], ~Inst[20]);  // AND_Gate
  and and_4 (and_4_out, ~Inst[27], ~Inst[26], ~Inst[25]);  // AND_Gate
  and and_5 (and_5_out, ~Inst[27], Inst[26], Inst[25]);  // AND_Gate
  assign bit_extender_1_out = {{1{Rot}}, Rot};  // Bit_Extender bit_extender_1
  assign bit_extender_2_out = {{1{Shift}}, Shift};  // Bit_Extender bit_extender_2
  or or_1 (Shift, and_4_out, and_5_out);
  assign and_6_out = bit_extender_1_out & {2{Rot}};  // AND_Gate and_6, 2 bits wide
  assign and_7_out = Inst[6:5] & bit_extender_2_out;  // AND_Gate and_7, 2 bits wide
  and and_8 (IsLd, Inst[27], ~Inst[26]);  // AND_Gate
  not not_1 (not_1_out[0], Rot);
  assign SOp = and_6_out | and_7_out;  // OR_Gate or_2, 2 bits wide
  assign bit_extender_3_out = {{4{Rot}}, Rot};  // Bit_Extender bit_extender_3
  assign Imm = {{24{1'b0}}, Inst[7:0]};  // Bit_Extender bit_extender_4
  assign SRimm = {Inst[11:8], not_1_out[0]} & bit_extender_3_out;  // AND_Gate and_9, 5 bits wide

  assign Rm = Inst[3:0];
  assign Rs = Inst[11:8];
  assign SrSi = Inst[4];

  // Other names for the same wires on the sheet: C[3:0] = Inst[31:28]; F[1:0] = Inst[27:26]; S = Inst[20];
  //   I = Inst[25]; O[3:0] = Inst[24:21]; Imm8[7:0] = Inst[7:0]; OP2[11:0] = Inst[11:0]; SRorSI = Inst[4];
  //   SOp_t[1:0] = Inst[6:5]; SI[4:0] = Inst[11:7]; RotImm[3:0] = Inst[11:8]; Rd[3:0] = Inst[15:12];
  //   Rn[3:0] = Inst[19:16]

  // Notes on the sheet:
  //   1 if register shift and 0 if shift immediate
  //   This includes rotates and shift imms
endmodule

module CPSRDecode (
  input  [31:0] Cspr,
  input  [3:0] Cond,
  output Execute
);

  wire AL, and_1_out, and_2_out, and_3_out, and_4_out, and_5_out, and_6_out, and_7_out, and_8_out, and_9_out,
       and_10_out, and_11_out, and_12_out, and_13_out, and_14_out, EQ, GE, GT, HI, HS, LE, LO, LS, LT, MI,
       NE, NV, or_1_out, or_2_out, or_3_out, or_4_out, or_5_out, or_6_out, or_7_out, or_8_out, or_9_out,
       or_10_out, or_11_out, or_12_out, or_13_out, PL, VC, VS;

  Decoder #(.select(4), .enable("false")) decoder_1 (
    .out0(EQ), .out1(NE), .out2(HS), .out3(LO), .out4(MI), .out5(PL), .out6(VS), .out7(VC), .out8(HI),
    .out9(LS), .out10(GE), .out11(LT), .out12(GT), .out13(LE), .out14(AL), .out15(NV), .sel(Cond));
  and and_1 (and_1_out, EQ, Cspr[30]);
  and and_2 (and_2_out, NE, ~Cspr[30]);  // AND_Gate
  and and_3 (and_3_out, HS, Cspr[29]);
  and and_4 (and_4_out, LO, ~Cspr[29]);  // AND_Gate
  and and_5 (and_5_out, MI, Cspr[31]);
  and and_6 (and_6_out, PL, ~Cspr[31]);  // AND_Gate
  and and_7 (and_7_out, VS, Cspr[28]);
  and and_8 (and_8_out, VC, ~Cspr[28]);  // AND_Gate
  and and_9 (and_9_out, HI, Cspr[29], ~Cspr[30]);  // AND_Gate
  or or_1 (or_1_out, ~Cspr[29], Cspr[30]);  // OR_Gate
  or or_2 (or_2_out, Cspr[28], Cspr[31]);
  or or_3 (or_3_out, ~Cspr[28], ~Cspr[31]);  // OR_Gate
  or or_4 (or_4_out, ~Cspr[28], Cspr[31]);  // OR_Gate
  or or_5 (or_5_out, Cspr[28], ~Cspr[31]);  // OR_Gate
  or or_6 (or_6_out, Cspr[28], ~Cspr[30], Cspr[31]);  // OR_Gate
  or or_7 (or_7_out, ~Cspr[28], ~Cspr[30], ~Cspr[31]);  // OR_Gate
  or or_8 (or_8_out, ~Cspr[28], Cspr[30], Cspr[31]);  // OR_Gate
  or or_9 (or_9_out, Cspr[28], Cspr[30], ~Cspr[31]);  // OR_Gate
  and and_10 (and_10_out, or_1_out, LS);
  or or_10 (or_10_out, or_2_out, or_3_out);
  or or_11 (or_11_out, or_4_out, or_5_out);
  or or_12 (or_12_out, or_6_out, or_7_out);
  or or_13 (or_13_out, or_8_out, or_9_out);
  and and_11 (and_11_out, or_10_out, GE);
  and and_12 (and_12_out, or_11_out, LT);
  and and_13 (and_13_out, or_12_out, GT);
  and and_14 (and_14_out, or_13_out, LE);
  or or_14 (Execute, and_1_out, and_2_out, and_3_out, and_4_out, and_5_out, and_6_out, and_7_out, and_8_out, and_9_out, and_10_out, and_11_out, and_12_out, and_13_out, and_14_out, AL);

  // Other names for the same wires on the sheet: b0 = Cspr[28]; b1 = Cspr[29]; b2 = Cspr[30]; b3 = Cspr[31]
endmodule

module RegFile (
  input  [31:0] cpsrIn,
  input  S,
  input  [31:0] W,
  input  WE,
  input  Clk,
  input  [3:0] rM,
  input  [3:0] rW,
  input  [3:0] rN,
  input  [3:0] rS,
  output [31:0] cpsrOut,
  output [31:0] M,
  output [31:0] N,
  output [4:0] SV
);

  wire and_1_out, and_2_out, and_3_out, and_4_out, and_5_out, and_6_out, and_7_out, and_8_out, and_9_out,
       and_10_out, and_11_out, and_12_out, and_13_out, and_14_out, and_15_out, r0, r1, r2, r3, r4, r5, r6,
       r7, r8, r9, r10, r11, r12, r13, r14;
  wire [31:0] a1, a2, a3, a4, ip, lr, sp, v1, v2, v3, v4, v5, v6, v7, v8;
  wire [31:5] multiplexer_3_out;

  Decoder #(.select(4), .enable("false")) decoder_1 (
    .out0(r0), .out1(r1), .out2(r2), .out3(r3), .out4(r4), .out5(r5), .out6(r6), .out7(r7), .out8(r8),
    .out9(r9), .out10(r10), .out11(r11), .out12(r12), .out13(r13), .out14(r14), .sel(rW));  // open: out15
  Register #(.width(32)) cpsr (.D(cpsrIn), .en(S), .clk(Clk), .Q(cpsrOut));  // open: clr
  Register #(.width(32)) u_a1 (.D(W), .en(and_1_out), .clk(Clk), .Q(a1));  // open: clr
  and and_1 (and_1_out, WE, r0);
  Register #(.width(32)) u_a2 (.D(W), .en(and_2_out), .clk(Clk), .Q(a2));  // open: clr
  and and_2 (and_2_out, WE, r1);
  Register #(.width(32)) u_a3 (.D(W), .en(and_3_out), .clk(Clk), .Q(a3));  // open: clr
  and and_3 (and_3_out, WE, r2);
  Register #(.width(32)) u_a4 (.D(W), .en(and_4_out), .clk(Clk), .Q(a4));  // open: clr
  and and_4 (and_4_out, WE, r3);
  Register #(.width(32)) u_v1 (.D(W), .en(and_5_out), .clk(Clk), .Q(v1));  // open: clr
  and and_5 (and_5_out, WE, r4);
  Register #(.width(32)) u_v2 (.D(W), .en(and_6_out), .clk(Clk), .Q(v2));  // open: clr
  and and_6 (and_6_out, WE, r5);
  Register #(.width(32)) u_v3 (.D(W), .en(and_7_out), .clk(Clk), .Q(v3));  // open: clr
  and and_7 (and_7_out, WE, r6);
  Register #(.width(32)) u_v4 (.D(W), .en(and_8_out), .clk(Clk), .Q(v4));  // open: clr
  and and_8 (and_8_out, WE, r7);
  Register #(.width(32)) u_v5 (.D(W), .en(and_9_out), .clk(Clk), .Q(v5));  // open: clr
  and and_9 (and_9_out, WE, r8);
  Register #(.width(32)) u_v6 (.D(W), .en(and_10_out), .clk(Clk), .Q(v6));  // open: clr
  and and_10 (and_10_out, WE, r9);
  Register #(.width(32)) u_v7 (.D(W), .en(and_11_out), .clk(Clk), .Q(v7));  // open: clr
  and and_11 (and_11_out, WE, r10);
  Register #(.width(32)) u_v8 (.D(W), .en(and_12_out), .clk(Clk), .Q(v8));  // open: clr
  and and_12 (and_12_out, WE, r11);
  Register #(.width(32)) u_ip (.D(W), .en(and_13_out), .clk(Clk), .Q(ip));  // open: clr
  and and_13 (and_13_out, WE, r12);
  Register #(.width(32)) u_sp (.D(W), .en(and_14_out), .clk(Clk), .Q(sp));  // open: clr
  and and_14 (and_14_out, WE, r13);
  Register #(.width(32)) u_lr (.D(W), .en(and_15_out), .clk(Clk), .Q(lr));  // open: clr
  and and_15 (and_15_out, WE, r14);
  Multiplexer #(.select(4), .width(32), .enable("false")) multiplexer_1 (
    .in0(a1), .in1(a2), .in2(a3), .in3(a4), .in4(v1), .in5(v2), .in6(v3), .in7(v4), .in8(v5), .in9(v6),
    .in10(v7), .in11(v8), .in12(ip), .in13(sp), .in14(lr), .out(M), .sel(rM));  // open: in15
  Multiplexer #(.select(4), .width(32), .enable("false")) multiplexer_2 (
    .in0(a1), .in1(a2), .in2(a3), .in3(a4), .in4(v1), .in5(v2), .in6(v3), .in7(v4), .in8(v5), .in9(v6),
    .in10(v7), .in11(v8), .in12(ip), .in13(sp), .in14(lr), .out(N), .sel(rN));  // open: in15
  Multiplexer #(.select(4), .width(32), .enable("false")) multiplexer_3 (
    .in0(a1), .in1(a2), .in2(a3), .in3(a4), .in4(v1), .in5(v2), .in6(v3), .in7(v4), .in8(v5), .in9(v6),
    .in10(v7), .in11(v8), .in12(ip), .in13(sp), .in14(lr), .out({multiplexer_3_out, SV}), .sel(rS));  // open: in15
endmodule

module DE (
  input  [31:0] M,
  input  [31:0] N,
  input  [31:0] ImmOff,
  input  [31:0] BAddr,
  input  I,
  input  [31:0] CPSR,
  input  [3:0] ALUOp,
  input  [3:0] Rd,
  input  [4:0] COND,
  input  [4:0] S,
  input  [4:0] SRimm,
  input  [4:0] ALUbit,
  input  [3:0] Shifts,
  input  [3:0] ToMem,
  input  [1:0] MEMOp,
  input  WE,
  input  CLK,
  output [31:0] Mo,
  output [31:0] No,
  output [31:0] Io,
  output [31:0] Ba,
  output I0,
  output [31:0] CPSRo,
  output [3:0] ALUOpo,
  output [3:0] Rdo,
  output [4:0] CONDo,
  output [4:0] So,
  output [4:0] SRimmo,
  output [4:0] ALUbitso,
  output [3:0] Shiftso,
  output [3:0] ToM,
  output [1:0] MOp
);

  Register #(.width(32)) register_1 (.D(M), .en(WE), .clk(CLK), .Q(Mo));  // open: clr
  Register #(.width(32)) register_2 (.D(N), .en(WE), .clk(CLK), .Q(No));  // open: clr
  Register #(.width(32)) register_3 (.D(ImmOff), .en(WE), .clk(CLK), .Q(Io));  // open: clr
  Register #(.width(32)) register_4 (.D(BAddr), .en(WE), .clk(CLK), .Q(Ba));  // open: clr
  Register #(.width(1)) register_5 (.D(I), .en(WE), .clk(CLK), .Q(I0));  // open: clr
  Register #(.width(32)) register_6 (.D(CPSR), .en(WE), .clk(CLK), .Q(CPSRo));  // open: clr
  Register #(.width(4)) register_7 (.D(ALUOp), .en(WE), .clk(CLK), .Q(ALUOpo));  // open: clr
  Register #(.width(4)) register_8 (.D(Rd), .en(WE), .clk(CLK), .Q(Rdo));  // open: clr
  Register #(.width(5)) register_9 (.D(S), .en(WE), .clk(CLK), .Q(So));  // open: clr
  Register #(.width(5)) register_10 (.D(SRimm), .en(WE), .clk(CLK), .Q(SRimmo));  // open: clr
  Register #(.width(5)) register_11 (.D(ALUbit), .en(WE), .clk(CLK), .Q(ALUbitso));  // open: clr
  Register #(.width(4)) register_12 (.D(Shifts), .en(WE), .clk(CLK), .Q(Shiftso));  // open: clr
  Register #(.width(4)) register_13 (.D(ToMem), .en(WE), .clk(CLK), .Q(ToM));  // open: clr
  Register #(.width(2)) register_14 (.D(MEMOp), .en(WE), .clk(CLK), .Q(MOp));  // open: clr
  Register #(.width(5)) register_15 (.D(COND), .en(WE), .clk(WE), .Q(CONDo));  // open: clr

  // Notes on the sheet:
  //   0 extend the immediate
endmodule

module Execute (
  input  [31:0] WbN,
  input  [31:0] MemN,
  input  [31:0] N,
  input  [31:0] M,
  input  [31:0] MemM,
  input  [31:0] WbM,
  input  [3:0] ALUOp,
  input  [3:0] Rd,
  input  [1:0] ForwardM,
  input  [1:0] ForwardN,
  input  [1:0] ShiftOp,
  input  [4:0] SA,
  input  SetCondFlag,
  output [31:0] C,
  output [3:0] COND,
  output SCF
);

  wire [31:0] mux3x1_1_a0;

  Mux3x1 mux3x1_1 (.SWBEX(ForwardM[1]), .WBA(WbM), .A(M), .MemA(MemM), .SMEX(ForwardM[0]), .A0(mux3x1_1_a0));
  ALU alu_1 (
    .WBN(WbN), .MemN(MemN), .N(N), .ForwardN(ForwardN), .M(mux3x1_1_a0), .ALUop(ALUOp), .C(C), .COND(COND));  // open: SA, ShOp

  assign SCF = SetCondFlag;
endmodule

module ShiftHandler (
  input  [31:0] M
);
endmodule

module ALU (
  input  [31:0] WBN,
  input  [31:0] MemN,
  input  [31:0] N,
  input  [1:0] ForwardN,
  input  [31:0] M,
  input  [3:0] ALUop,
  input  [4:0] SA,
  input  [1:0] ShOp,
  output [31:0] C,
  output [3:0] COND
);

  wire [31:0] mux3x1_1_a0;

  Mux3x1 mux3x1_1 (.SWBEX(ForwardN[1]), .WBA(WBN), .A(N), .MemA(MemN), .SMEX(ForwardN[0]), .A0(mux3x1_1_a0));
  // ARM_ALU arm_alu_1: pin names not known; wires that end beside it: mux3x1_1_a0, M, ALUop, SA, ShOp, C, COND
endmodule

module HB (
  input  [4:0] ExMemRd,
  input  [4:0] IdExRa,
  input  [4:0] IdExRb,
  input  [4:0] MemWbRd,
  input  Im0,
  input  EnablM,
  input  MovM,
  input  EnblW,
  input  MovW,
  output out_10,
  output out_11,
  output out_12,
  output out_13
);

  wire and_1_out, and_2_out, and_3_out, and_4_out, and_5_out, and_6_out, and_7_out, and_8_out, and_9_out,
       and_10_out, eq_1_eq, eq_2_eq, eq_3_eq, eq_4_eq, nand_1_out, nand_2_out, or_1_out, or_2_out;

  or or_1 (or_1_out, ExMemRd[0], ExMemRd[1], ExMemRd[2], ExMemRd[3], ExMemRd[4]);
  EQ eq_1 (.A(ExMemRd), .B(IdExRa), .EQ(eq_1_eq));
  EQ eq_2 (.A(ExMemRd), .B(IdExRb), .EQ(eq_2_eq));
  or or_2 (or_2_out, MemWbRd[0], MemWbRd[1], MemWbRd[2], MemWbRd[3], MemWbRd[4]);
  EQ eq_3 (.A(MemWbRd), .B(IdExRa), .EQ(eq_3_eq));
  EQ eq_4 (.A(MemWbRd), .B(IdExRb), .EQ(eq_4_eq));
  and and_1 (and_1_out, or_1_out, eq_1_eq);
  and and_2 (and_2_out, or_1_out, eq_2_eq);
  nand nand_1 (nand_1_out, or_1_out, eq_1_eq);
  and and_3 (and_3_out, nand_1_out, or_2_out, eq_3_eq);
  nand nand_2 (nand_2_out, or_1_out, eq_2_eq);
  and and_4 (and_4_out, nand_2_out, or_2_out, eq_4_eq);
  and and_5 (and_5_out, and_2_out, ~Im0);  // AND_Gate
  and and_6 (and_6_out, ~Im0, and_4_out);  // AND_Gate
  and and_7 (and_7_out, and_1_out, MovM);
  and and_8 (and_8_out, and_5_out, MovM);
  and and_9 (and_9_out, and_3_out, MovW);
  and and_10 (and_10_out, and_6_out, MovW);
  Multiplexer #(.enable("false")) multiplexer_1 (.in0(and_1_out), .in1(and_7_out), .out(out_10), .sel(EnablM));
  Multiplexer #(.enable("false")) multiplexer_2 (.in0(and_5_out), .in1(and_8_out), .out(out_11), .sel(EnablM));
  Multiplexer #(.enable("false")) multiplexer_3 (.in0(and_3_out), .in1(and_9_out), .out(out_12), .sel(EnblW));
  Multiplexer #(.enable("false")) multiplexer_4 (.in0(and_6_out), .in1(and_10_out), .out(out_13), .sel(EnblW));
endmodule

module Shift (
  input  [31:0] M,
  input  [4:0] S,
  input  [1:0] SOp,
  output [31:0] Mn
);

  wire and_1_out, and_2_out, multiplexer_1_out, or_1_out, or_2_out, xor_1_out;
  wire [31:0] ls_1_mn, multiplexer_2_out, switch_1_mn, switch_2_mn;

  xor xor_1 (xor_1_out, SOp[0], SOp[0]);
  Switch switch_1 (.M(M), .Mn(switch_1_mn));
  Multiplexer #(.enable("false")) multiplexer_1 (
    .in0(xor_1_out), .in1(M[31]), .out(multiplexer_1_out), .sel(and_1_out));
  and and_1 (and_1_out, ~SOp[0], SOp[1]);  // AND_Gate
  Multiplexer #(.width(32), .enable("false")) multiplexer_2 (
    .in0(M), .in1(switch_1_mn), .out(multiplexer_2_out), .sel(or_1_out));
  or or_1 (or_1_out, SOp[0], SOp[1]);
  and and_2 (and_2_out, SOp[0], SOp[1]);
  LS ls_1 (.M(multiplexer_2_out), .S(S), .C(multiplexer_1_out), .R(and_2_out), .Mn(ls_1_mn));
  Multiplexer #(.width(32), .enable("false")) multiplexer_3 (
    .in0(ls_1_mn), .in1(switch_2_mn), .out(Mn), .sel(or_2_out));
  Switch switch_2 (.M(ls_1_mn), .Mn(switch_2_mn));
  or or_2 (or_2_out, SOp[0], SOp[1]);
endmodule

module LS (
  input  [31:0] M,
  input  [4:0] S,
  input  C,
  input  R,
  output [31:0] Mn
);

  wire [31:0] l2_1_mn, l4_1_mn, l8_1_mn, l16_1_mn;

  L16 l16_1 (.M(M), .S(S[4]), .C(C), .R(R), .Mn(l16_1_mn));
  L8 l8_1 (.M(l16_1_mn), .S(S[3]), .C(C), .R(R), .Mn(l8_1_mn));
  L4 l4_1 (.M(l8_1_mn), .S(S[2]), .C(C), .R(R), .Mn(l4_1_mn));
  L2 l2_1 (.M(l4_1_mn), .S(S[1]), .C(C), .R(R), .Mn(l2_1_mn));
  L1 l1_1 (.M(l2_1_mn), .S(S[0]), .C(C), .R(R), .Mn(Mn));
endmodule

module L1 (
  input  [31:0] M,
  input  S,
  input  C,
  input  R,
  output [31:0] Mn
);

  wire [0:0] multiplexer_1_out;

  Multiplexer #(.enable("false")) multiplexer_1 (.in0(C), .in1(M[31]), .out(multiplexer_1_out[0]), .sel(R));
  Multiplexer #(.width(32), .enable("false")) multiplexer_2 (
    .in0(M), .in1({M[30:0], multiplexer_1_out[0]}), .out(Mn), .sel(S));
endmodule

module L2 (
  input  [31:0] M,
  input  S,
  input  C,
  input  R,
  output [31:0] Mn
);

  wire [1:0] bit_extender_1_out, multiplexer_1_out;

  assign bit_extender_1_out = {{1{C}}, C};  // Bit_Extender bit_extender_1
  Multiplexer #(.width(2), .enable("false")) multiplexer_1 (
    .in0(bit_extender_1_out), .in1({M[30], M[31]}), .out(multiplexer_1_out), .sel(R));
  Multiplexer #(.width(32), .enable("false")) multiplexer_2 (
    .in0(M), .in1({M[29:0], multiplexer_1_out[0], multiplexer_1_out[1]}), .out(Mn), .sel(S));
endmodule

module L4 (
  input  [31:0] M,
  input  S,
  input  C,
  input  R,
  output [31:0] Mn
);

  wire [3:0] bit_extender_1_out, multiplexer_1_out;

  assign bit_extender_1_out = {{3{C}}, C};  // Bit_Extender bit_extender_1
  Multiplexer #(.width(4), .enable("false")) multiplexer_1 (
    .in0(bit_extender_1_out), .in1({M[28], M[29], M[30], M[31]}), .out(multiplexer_1_out), .sel(R));
  Multiplexer #(.width(32), .enable("false")) multiplexer_2 (
    .in0(M),
    .in1({M[27:0], multiplexer_1_out[0], multiplexer_1_out[1], multiplexer_1_out[2], multiplexer_1_out[3]}),
    .out(Mn), .sel(S));
endmodule

module L8 (
  input  [31:0] M,
  input  S,
  input  C,
  input  R,
  output [31:0] Mn
);

  wire [7:0] bit_extender_1_out, multiplexer_1_out;

  assign bit_extender_1_out = {{7{C}}, C};  // Bit_Extender bit_extender_1
  Multiplexer #(.width(8), .enable("false")) multiplexer_1 (
    .in0(bit_extender_1_out), .in1({M[24], M[25], M[26], M[27], M[28], M[29], M[30], M[31]}),
    .out(multiplexer_1_out), .sel(R));
  Multiplexer #(.width(32), .enable("false")) multiplexer_2 (
    .in0(M),
    .in1({M[23:0], multiplexer_1_out[0], multiplexer_1_out[1], multiplexer_1_out[2], multiplexer_1_out[3], multiplexer_1_out[4], multiplexer_1_out[5], multiplexer_1_out[6], multiplexer_1_out[7]}),
    .out(Mn), .sel(S));
endmodule

module L16 (
  input  [31:0] M,
  input  S,
  input  C,
  input  R,
  output [31:0] Mn
);

  wire [15:0] bit_extender_1_out, multiplexer_1_out;

  assign bit_extender_1_out = {{15{C}}, C};  // Bit_Extender bit_extender_1
  Multiplexer #(.width(16), .enable("false")) multiplexer_1 (
    .in0(bit_extender_1_out),
    .in1({M[16], M[17], M[18], M[19], M[20], M[21], M[22], M[23], M[24], M[25], M[26], M[27], M[28], M[29], M[30], M[31]}),
    .out(multiplexer_1_out), .sel(R));
  Multiplexer #(.width(32), .enable("false")) multiplexer_2 (
    .in0(M),
    .in1({M[15:0], multiplexer_1_out[0], multiplexer_1_out[1], multiplexer_1_out[2], multiplexer_1_out[3], multiplexer_1_out[4], multiplexer_1_out[5], multiplexer_1_out[6], multiplexer_1_out[7], multiplexer_1_out[8], multiplexer_1_out[9], multiplexer_1_out[10], multiplexer_1_out[11], multiplexer_1_out[12], multiplexer_1_out[13], multiplexer_1_out[14], multiplexer_1_out[15]}),
    .out(Mn), .sel(S));
endmodule

module Switch (
  input  [31:0] M,
  output [31:0] Mn
);


  assign Mn = {M[0], M[1], M[2], M[3], M[4], M[5], M[6], M[7], M[8], M[9], M[10], M[11], M[12], M[13], M[14], M[15], M[16], M[17], M[18], M[19], M[20], M[21], M[22], M[23], M[24], M[25], M[26], M[27], M[28], M[29], M[30], M[31]};
endmodule

module Mux3x1 (
  input  [31:0] A,
  input  [31:0] MemA,
  input  [31:0] WBA,
  input  SMEX,
  input  SWBEX,
  output [31:0] A0
);

  wire [31:0] multiplexer_1_out;

  Multiplexer #(.width(32), .enable("false")) multiplexer_1 (.in0(A), .in1(MemA), .out(multiplexer_1_out), .sel(SMEX));
  Multiplexer #(.width(32), .enable("false")) multiplexer_2 (.in0(multiplexer_1_out), .in1(WBA), .out(A0), .sel(SWBEX));
endmodule

module EQ (
  input  [4:0] A,
  input  [4:0] B,
  output EQ
);

  wire [4:0] xnor_1_out;

  assign xnor_1_out = ~(A ^ B);  // XNOR_Gate xnor_1, 5 bits wide
  and and_1 (EQ, xnor_1_out[0], xnor_1_out[1], xnor_1_out[2], xnor_1_out[3], xnor_1_out[4]);
endmodule

module PCincr (
  input  [31:0] PC,
  output [31:0] PC4
);

  // Incrementer #(.width(30)) incrementer_1: pin names not known; wires that end beside it: PC[31:2], PC4[31:2]

  assign PC4[1:0] = PC[1:0];
endmodule
