// Logisim project cpu_2.circ as structural Verilog: 30 circuits, main circuit main
module main (
);

  wire and_1_out, and_2_out, BL, BraSel, CLK, memory_1_branch, memory_1_store, mw_1_b_o, mw_1_str_o,
       not_1_out, not_2_out, Stall, Zap;
  wire [1:0] FM, FN, FS;
  wire [3:0] em_1_out_rd, execute_1_out_rd, memory_1_out_rd, mw_1_out_rd, r0, Rd, Rm, Rn, Rs;
  wire [4:0] decode_1_out_sri, em_1_out_res, mw_1_out_res, SA;
  wire [5:0] de_1_out_shift, decode_1_out_mem, decode_1_out_shift, em_1_out_flags, em_1_out_memop, Flag,
       flag_o, mem_0, memory_1_out_flags, mw_1_out_flags;
  wire [6:0] a3, a4, ALU, alu_0, memory_1_out_aluop;
  wire [11:0] decode_1_out_reg, execute_1_out_reg, r3, Reg_o;
  wire [31:0] Addr_o, armprogramrom_1_p1, BAddr, c3, cpsr, de_1_out_cpsr, decode_1_out_addr,
       decode_1_out_imm, em_1_out_data, execute_1_c, execute_1_out_addr, execute_1_out_cpsr,
       execute_1_out_data, fd_1_inst_o, fd_1_pc_o, Imm_o, M, memory_1_out_cpsr, memory_1_out_resstore,
       multiplexer_1_out, multiplexer_2_out, mw_1_out_cpsr, N, pc1, PC_q, pcincr_1_pc4, regfile_1_cpsrout,
       regfile_1_m, regfile_1_n, regfile_1_sv, S;
  wire [31:5] em_1_out_res_2, mw_1_out_res_2;

  Register #(.width(32)) PC (.D(multiplexer_1_out), .en(Stall), .clk(CLK), .Q(PC_q));  // open: clr
  // ARMProgramROM armprogramrom_1: pin names not known; wires that end beside it: armprogramrom_1_p1
  Clock u_CLK (.out(CLK));
  Multiplexer #(.width(32), .enable("false")) multiplexer_1 (
    .in0(BAddr), .in1(pcincr_1_pc4), .out(multiplexer_1_out), .sel(not_1_out));
  not not_1 (not_1_out, BraSel);
  PCincr pcincr_1 (.PC(PC_q), .PC4(pcincr_1_pc4));
  not not_2 (not_2_out, mw_1_out_flags[4]);
  FD fd_1 (
    .Inst(armprogramrom_1_p1), .PC(pcincr_1_pc4), .R(Zap), .WE(Stall), .CLK(CLK), .Inst_o(fd_1_inst_o),
    .PC_o(fd_1_pc_o));
  Multiplexer #(.width(32), .enable("false")) multiplexer_2 (
    .in0(mw_1_out_cpsr), .in1(c3), .out(multiplexer_2_out), .sel(not_2_out));
  and and_1 (and_1_out, and_2_out, ~mw_1_b_o);  // AND_Gate
  and and_2 (and_2_out, ~mw_1_out_flags[1], ~mw_1_str_o, a4[6]);  // AND_Gate
  Decode decode_1 (
    .Inst(fd_1_inst_o), .CPSR(regfile_1_cpsrout), .CPSR_F(multiplexer_2_out), .CPSR_fbit(em_1_out_flags[4]),
    .PC(fd_1_pc_o), .Out_Flags(Flag), .Out_Shift(decode_1_out_shift), .Out_SRI(decode_1_out_sri),
    .Out_Imm(decode_1_out_imm), .Out_Addr(decode_1_out_addr), .Out_Mem(decode_1_out_mem), .Out_BL(BL),
    .Out_ALU(ALU), .Out_CPSR(cpsr), .Rn(Rn), .Rm(Rm), .Rs(Rs), .Rd(r0), .Out_Reg(decode_1_out_reg), .PC_o(pc1));
  RegFile regfile_1 (
    .W({mw_1_out_res_2, mw_1_out_res}), .cpsrIn(mw_1_out_cpsr), .Clk(CLK), .rW(mw_1_out_rd),
    .cpsrOut(regfile_1_cpsrout), .rN(Rn), .rM(Rm), .M(regfile_1_m), .WE(and_1_out), .S(mw_1_out_flags[4]),
    .N(regfile_1_n), .SV(regfile_1_sv), .rS(Rs));
  BranchStall branchstall_1 (
    .ALU_De(ALU), .In_Addr(decode_1_out_addr), .PC(pc1), .In_BL(BL), .MEM(mem_0), .Rn(Rn), .Rm(Rm),
    .Rd(execute_1_out_rd), .ALU_Ex(alu_0), .Branch(BraSel), .Out_addr(BAddr), .Zap(Zap), .Stall(Stall));
  DE de_1 (
    .M(regfile_1_m), .N(regfile_1_n), .S(regfile_1_sv), .In_Imm(decode_1_out_imm), .In_Addr(pc1), .In_BL(BL),
    .In_Shift(decode_1_out_shift), .In_CPSR(cpsr), .In_ALU(ALU), .Rd(r0), .In_Mem(decode_1_out_mem),
    .In_Flags(Flag), .In_SRI(decode_1_out_sri), .In_Reg(decode_1_out_reg), .St(Stall), .WE(1'b1), .CLK(CLK),
    .Mo(M), .No(N), .So(S), .Out_Imm(Imm_o), .Out_Addr(Addr_o), .Out_BL(BL), .Out_Shift(de_1_out_shift),
    .Out_CPSR(de_1_out_cpsr), .Out_ALU(alu_0), .Rdo(Rd), .Out_Mem(mem_0), .Out_Flags(flag_o), .Out_SRI(SA),
    .Out_Reg(Reg_o));
  Hazard hazard_1 (
    .M_Ex_D(em_1_out_rd), .W_Ex_D(mw_1_out_rd), .In_ExecuteR(Reg_o), .In_Shift(de_1_out_shift), .EnblM(a3),
    .EnblW(a4), .ForwardN(FN), .ForwardM(FM), .ForwardS(FS));
  Execute execute_1 (
    .N(N), .MemN({em_1_out_res_2, em_1_out_res}), .WbN({mw_1_out_res_2, mw_1_out_res}), .M(M),
    .MemM({em_1_out_res_2, em_1_out_res}), .WbM({mw_1_out_res_2, mw_1_out_res}), .ForwardN(FN),
    .ForwardM(FM), .ForwardS(FS), .In_ALU(alu_0), .In_SRI(SA), .In_Shift(de_1_out_shift), .In_Flags(flag_o),
    .In_Mem(mem_0), .In_Rd(Rd), .In_CPSR(de_1_out_cpsr), .In_Imm(Imm_o), .In_Addr(Addr_o), .S(S),
    .MemS(em_1_out_res), .WbS(mw_1_out_res), .In_Reg(Reg_o), .BL(BL), .C(execute_1_c),
    .Out_CPSR(execute_1_out_cpsr), .Out_Addr(execute_1_out_addr), .Out_Rd(execute_1_out_rd),
    .Out_Reg(execute_1_out_reg), .Out_Data(execute_1_out_data));
  EM em_1 (
    .In_Res(execute_1_c), .In_Addr(execute_1_out_addr), .In_MemOp(mem_0), .In_Rd(execute_1_out_rd),
    .In_AlLUOp(alu_0), .In_Reg(execute_1_out_reg), .In_CPSR(execute_1_out_cpsr), .In_Flags(flag_o),
    .In_Data(execute_1_out_data), .WE(1'b1), .CLK(CLK), .Out_Res({em_1_out_res_2, em_1_out_res}),
    .Out_MemOp(em_1_out_memop), .Out_Rd(em_1_out_rd), .Out_ALUOp(a3), .Out_Reg(r3), .Out_CPSR(c3),
    .Out_Flags(em_1_out_flags), .Out_Data(em_1_out_data));  // open: Out_Addr
  Memory memory_1 (
    .In_Res({em_1_out_res_2, em_1_out_res}), .In_Data(em_1_out_data), .In_MemOp(em_1_out_memop),
    .In_ALUOp(a3), .In_Rd(em_1_out_rd), .In_CPSR(c3), .In_Flags(em_1_out_flags), .CLK(CLK),
    .Out_ResStore(memory_1_out_resstore), .Out_Rd(memory_1_out_rd), .Out_Flags(memory_1_out_flags),
    .Out_CPSR(memory_1_out_cpsr), .out_ALUOp(memory_1_out_aluop), .store(memory_1_store),
    .Branch(memory_1_branch));
  MW mw_1 (
    .In_Res(memory_1_out_resstore), .In_Rd(memory_1_out_rd), .In_Flags(memory_1_out_flags), .In_Reg(r3),
    .In_CPSR(memory_1_out_cpsr), .In_ALU(memory_1_out_aluop), .str(memory_1_store), .B(memory_1_branch),
    .WE(1'b1), .CLK(CLK), .Out_Res({mw_1_out_res_2, mw_1_out_res}), .Out_Rd(mw_1_out_rd),
    .Out_Flags(mw_1_out_flags), .Out_CPSR(mw_1_out_cpsr), .Out_ALU(a4), .str_o(mw_1_str_o), .B_o(mw_1_b_o));  // open: Out_Reg

  // Notes on the sheet:
  //   contents of armprogramrom_1 (hex, n*v repeats v):
  //   mov a1, #&1 mov a2, #&1  @ Hazard testing adds a3, a1, a2, lsl #&5 adds a4, a1, a3, lsr #&5 adds v1,
  //   a4, a3, lsr #&5 subs v2, a4, v1  rsb v3, v2, v1  @ Loads and Stores with Hazards str a3, [v3, a4,
  //   lsl #&1] ldr v4, [a1, #&7] sub v4, v4, #&1  @ Conditional Execution subeq v5, a3, a4 subne v6, a3,
  //   a4 cmp v6, v5  @ Branch b next add a1, a1, #&1 @ fodder add a1, a1, #&1 add a1, a1, #&1 add a1, a1,
  //   #&1 add a1, a1, #&1 next: sub a1, a1, #&2
  //   scf flag to indicate need for forwarding
  //   forwarded cpsr
  //   takes address from decode and if execute then branch and then deal with stalls and shit
  //   if cmp then WE == 0
  //   still needs work
  //   need someway            of handling no reg shift into reg file
  //   Forwarding Path Mem -> Ex
  //   Forwarding Path WB -> Ex
  //   32 /-> 5 bit legacy splitters
endmodule

module FD (
  input  [31:0] Inst,
  input  [31:0] PC,
  input  R,
  input  WE,
  input  CLK,
  output [31:0] Inst_o,
  output [31:0] PC_o
);

  wire not_1_out;
  wire [31:0] bit_extender_1_out;

  not not_1 (not_1_out, R);
  assign bit_extender_1_out = {{31{not_1_out}}, not_1_out};  // Bit_Extender bit_extender_1
  Register #(.width(32)) register_1 (.D(Inst), .en(WE), .clk(CLK), .Q(Inst_o));  // open: clr
  Register #(.width(32)) register_2 (.D(PC), .en(WE), .clk(CLK), .Q(PC_o));  // open: clr
endmodule

module Decode (
  input  [31:0] Inst,
  input  [31:0] CPSR,
  input  [31:0] CPSR_F,
  input  CPSR_fbit,
  input  [31:0] PC,
  output [5:0] Out_Flags,
  output [5:0] Out_Shift,
  output [4:0] Out_SRI,
  output [31:0] Out_Imm,
  output [31:0] Out_Addr,
  output [5:0] Out_Mem,
  output Out_BL,
  output [6:0] Out_ALU,
  output [31:0] Out_CPSR,
  output [3:0] Rn,
  output [3:0] Rm,
  output [3:0] Rs,
  output [3:0] Rd,
  output [11:0] Out_Reg,
  output [31:0] PC_o
);

  wire and_1_out, and_2_out, and_3_out, and_4_out, and_5_out, and_6_out, op2decode_1_isld;
  wire [0:0] not_1_out;
  wire [3:0] aludecode_1_alu_op, memdecode_1_aluop;
  wire [31:0] bit_extender_1_out, demultiplexer_1_out0, demultiplexer_1_out1, demultiplexer_1_out2,
       op2decode_1_imm;

  Demultiplexer #(.select(2), .width(32), .enable("false")) demultiplexer_1 (
    .out0(demultiplexer_1_out0), .out1(demultiplexer_1_out1), .out2(demultiplexer_1_out2), .in(Inst),
    .sel(Inst[27:26]));  // open: out3
  PCincr pcincr_1 (.PC(PC), .PC4(PC_o));
  Multiplexer #(.width(32), .enable("false")) multiplexer_1 (.in0(CPSR), .in1(CPSR_F), .out(Out_CPSR), .sel(CPSR_fbit));
  OP2decode op2decode_1 (
    .Inst(Inst), .IsLd(op2decode_1_isld), .SRimm(Out_SRI), .Imm(op2decode_1_imm), .Rot(Out_Shift[1]),
    .SOp(Out_Shift[3:2]), .Shift(Out_Shift[0]), .Rm(Out_Reg[7:4]), .Rs(Out_Reg[3:0]), .SrSi(Out_Shift[5]));
  ALUDecode aludecode_1 (
    .Rev(Out_Flags[3]), .Cmp(Out_Flags[1]), .Neg(Out_Flags[5]), .SCF(demultiplexer_1_out0[20]),
    .Op(demultiplexer_1_out0[24:21]), .Mov(Out_Flags[0]), .Car(Out_Flags[2]), .S(Out_Flags[4]),
    .ALU_op(aludecode_1_alu_op));
  MEMdecode memdecode_1 (
    .OpCode({demultiplexer_1_out1[20], demultiplexer_1_out1[21], demultiplexer_1_out1[22], demultiplexer_1_out1[23], demultiplexer_1_out1[24]}),
    .ALUOp(memdecode_1_aluop), .PostAddr(Out_Mem[0]), .Norm(Out_Mem[3]), .OffAddr(Out_Mem[1]),
    .PreAddr(Out_Mem[2]), .MEMOp(Out_Mem[5:4]));
  BRAdecode bradecode_1 (
    .Cond(Inst[31:28]), .Link(Out_BL), .LorH(demultiplexer_1_out2[24]), .PC(PC_o),
    .One(demultiplexer_1_out2[25]), .Baddr(Inst[23:0]), .MAddr(Out_Addr));
  CPSRDecode cpsrdecode_1 (.Execute(Out_ALU[6]), .Cond(Inst[31:28]), .Cspr(Out_CPSR));
  Multiplexer #(.select(2), .width(4), .enable("false")) multiplexer_2 (
    .in0(aludecode_1_alu_op), .in1(memdecode_1_aluop), .out(Out_ALU[3:0]), .sel(Inst[27:26]));  // open: in2, in3
  assign bit_extender_1_out = {{20{1'b0}}, Inst[11:0]};  // Bit_Extender bit_extender_1
  and and_1 (and_1_out, Inst[26], ~Inst[27], ~Inst[25]);  // AND_Gate
  and and_2 (and_2_out, ~Inst[26], ~Inst[27], Inst[25]);  // AND_Gate
  or or_1 (Out_Shift[4], and_1_out, and_2_out, and_3_out);
  and and_3 (and_3_out, ~Inst[26], Inst[27], Inst[25]);  // AND_Gate
  Multiplexer #(.width(32), .enable("false")) multiplexer_3 (
    .in0(op2decode_1_imm), .in1(bit_extender_1_out), .out(Out_Imm), .sel(op2decode_1_isld));
  and and_4 (and_4_out, Inst[26], ~Inst[27]);  // AND_Gate
  and and_5 (and_5_out, and_4_out, ~Out_Mem[5]);  // AND_Gate
  Multiplexer #(.width(4), .enable("false")) multiplexer_4 (
    .in0(Inst[15:12]), .in1({{3{Inst[27]}}, not_1_out[0]}), .out(Rd), .sel(and_6_out));
  not not_1 (not_1_out[0], Inst[27]);
  and and_6 (and_6_out, ~Inst[26], Inst[27], Out_BL);  // AND_Gate
  Multiplexer #(.width(4), .enable("false")) multiplexer_5 (
    .in0(Out_Reg[3:0]), .in1(Inst[15:12]), .out(Rs), .sel(and_5_out));

  assign Out_ALU[5:4] = Inst[27:26];
  assign Out_Reg[11:8] = Inst[19:16];
  assign Rm = Out_Reg[7:4];
  assign Rn = Inst[19:16];

  // Other names for the same wires on the sheet: Baddr[23:0] = Inst[23:0]; Op2[11:0] = Inst[11:0];
  //   Rd_t[3:0] = Inst[15:12]; C[3:0] = Inst[31:28]; I = Inst[25]; F[1:0] = Inst[27:26]; Ex = Out_ALU[6];
  //   ToAddr[3:0] = Out_Mem[3:0]; MEMOp[1:0] = Out_Mem[5:4]; s[3:0] = Out_Reg[3:0]; Shift = Out_Shift[0];
  //   Rot = Out_Shift[1]; SOp[1:0] = Out_Shift[3:2]; SrSi = Out_Shift[5]; PC_t[31:0] = PC_o

  // Notes on the sheet:
  //   data proccessing 
  //   Loads and stores
  //   branches
  //   This is the neg output
  //   Type of Addressing Mode
  //   if branch link then rd is Link Reg
  //   0,1,2,3,4,5
  //   shift?, rotate?, shift op?, Imm, shift reg
  //   mov, cmp, car, rev, scf
  //   0,1,2,3,4
  //   ex, f, aluop
  //   Rn, Rm, Rs
endmodule

module ALUDecode (
  input  SCF,
  input  [3:0] Op,
  output Neg,
  output Mov,
  output Cmp,
  output Car,
  output Rev,
  output S,
  output [3:0] ALU_op
);

  wire [3:0] adc_o_out, add_o_out, and_o_out, bic_o_out, bit_extender_1_out, bit_extender_2_out,
       bit_extender_3_out, bit_extender_4_out, bit_extender_5_out, bit_extender_6_out, bit_extender_7_out,
       bit_extender_8_out, bit_extender_9_out, bit_extender_10_out, bit_extender_11_out, bit_extender_12_out,
       bit_extender_13_out, bit_extender_14_out, bit_extender_15_out, bit_extender_16_out, cmn_o_out,
       cmp_o_out, eor_o_out, mov_o_out, mvn_o_out, not_17_out, orr_o_out, rsb_o_out, rsc_o_out, sbc_o_out,
       sub_o_out, teq_o_out, tst_o_out;
  wire [3:1] decoder_1_out1, not_5_out, not_7_out, not_8_out, not_9_out, not_11_out, not_13_out, not_19_out,
       not_20_out, not_22_out, not_23_out, not_25_out;
  wire [3:2] decoder_1_out0, decoder_1_out8, decoder_1_out14;

  or or_1 (Neg, decoder_1_out14[2], not_25_out[3]);
  or or_2 (Mov, not_23_out[3], not_25_out[3]);
  or or_3 (Cmp, not_17_out[2], not_19_out[3], not_20_out[3], decoder_1_out8[2]);
  or or_4 (Car, not_11_out[3], not_13_out[3], not_9_out[3]);
  or or_5 (Rev, not_7_out[3], not_13_out[3]);
  Decoder #(.select(4), .enable("false")) decoder_1 (
    .out0(decoder_1_out0[2]), .out1(decoder_1_out1[1]), .out2(not_5_out[3]), .out3(not_7_out[3]),
    .out4(not_8_out[3]), .out5(not_9_out[3]), .out6(not_11_out[3]), .out7(not_13_out[3]),
    .out8(decoder_1_out8[2]), .out9(not_17_out[2]), .out10(not_19_out[3]), .out11(not_20_out[3]),
    .out12(not_22_out[2]), .out13(not_23_out[3]), .out14(decoder_1_out14[2]), .out15(not_25_out[3]), .sel(Op));
  assign bit_extender_1_out = {{3{decoder_1_out0[2]}}, decoder_1_out0[2]};  // Bit_Extender bit_extender_1
  assign and_o_out = bit_extender_1_out & ~{decoder_1_out0, {2{decoder_1_out0[2]}}};  // AND_Gate and_o, 4 bits wide
  not not_1 (decoder_1_out0[3], decoder_1_out0[2]);
  assign bit_extender_2_out = {{3{decoder_1_out1[1]}}, decoder_1_out1[1]};  // Bit_Extender bit_extender_2
  assign eor_o_out = bit_extender_2_out & ~{decoder_1_out1, decoder_1_out1[1]};  // AND_Gate eor_o, 4 bits wide
  not not_2 (decoder_1_out1[3], decoder_1_out1[1]);
  not not_3 (decoder_1_out1[2], decoder_1_out1[1]);
  assign bit_extender_3_out = {{3{not_5_out[3]}}, not_5_out[3]};  // Bit_Extender bit_extender_3
  assign sub_o_out = bit_extender_3_out & ~{not_5_out, not_5_out[3]};  // AND_Gate sub_o, 4 bits wide
  not not_4 (not_5_out[2], not_5_out[3]);
  not not_5 (not_5_out[1], not_5_out[3]);
  assign bit_extender_4_out = {{3{not_7_out[3]}}, not_7_out[3]};  // Bit_Extender bit_extender_4
  assign rsb_o_out = bit_extender_4_out & ~{not_7_out, not_7_out[3]};  // AND_Gate rsb_o, 4 bits wide
  not not_6 (not_7_out[2], not_7_out[3]);
  not not_7 (not_7_out[1], not_7_out[3]);
  assign bit_extender_5_out = {{3{not_8_out[3]}}, not_8_out[3]};  // Bit_Extender bit_extender_5
  assign add_o_out = bit_extender_5_out & ~{{2{not_8_out[3]}}, not_8_out[1], not_8_out[3]};  // AND_Gate add_o, 4 bits wide
  not not_8 (not_8_out[1], not_8_out[3]);
  assign bit_extender_6_out = {{3{not_9_out[3]}}, not_9_out[3]};  // Bit_Extender bit_extender_6
  assign adc_o_out = bit_extender_6_out & ~{{2{not_9_out[3]}}, not_9_out[1], not_9_out[3]};  // AND_Gate adc_o, 4 bits wide
  not not_9 (not_9_out[1], not_9_out[3]);
  assign bit_extender_7_out = {{3{not_11_out[3]}}, not_11_out[3]};  // Bit_Extender bit_extender_7
  assign sbc_o_out = bit_extender_7_out & ~{not_11_out, not_11_out[3]};  // AND_Gate sbc_o, 4 bits wide
  not not_10 (not_11_out[2], not_11_out[3]);
  not not_11 (not_11_out[1], not_11_out[3]);
  assign bit_extender_8_out = {{3{not_13_out[3]}}, not_13_out[3]};  // Bit_Extender bit_extender_8
  assign rsc_o_out = bit_extender_8_out & ~{not_13_out, not_13_out[3]};  // AND_Gate rsc_o, 4 bits wide
  not not_12 (not_13_out[2], not_13_out[3]);
  not not_13 (not_13_out[1], not_13_out[3]);
  assign bit_extender_9_out = {{3{decoder_1_out8[2]}}, decoder_1_out8[2]};  // Bit_Extender bit_extender_9
  assign tst_o_out = bit_extender_9_out & ~{decoder_1_out8, {2{decoder_1_out8[2]}}};  // AND_Gate tst_o, 4 bits wide
  not not_14 (decoder_1_out8[3], decoder_1_out8[2]);
  assign bit_extender_10_out = {{3{not_17_out[2]}}, not_17_out[2]};  // Bit_Extender bit_extender_10
  assign teq_o_out = bit_extender_10_out & ~not_17_out;  // AND_Gate teq_o, 4 bits wide
  not not_15 (not_17_out[3], not_17_out[2]);
  not not_16 (not_17_out[1], not_17_out[2]);
  not not_17 (not_17_out[0], not_17_out[2]);
  assign bit_extender_11_out = {{3{not_19_out[3]}}, not_19_out[3]};  // Bit_Extender bit_extender_11
  assign cmp_o_out = bit_extender_11_out & ~{not_19_out, not_19_out[3]};  // AND_Gate cmp_o, 4 bits wide
  not not_18 (not_19_out[2], not_19_out[3]);
  not not_19 (not_19_out[1], not_19_out[3]);
  assign bit_extender_12_out = {{3{not_20_out[3]}}, not_20_out[3]};  // Bit_Extender bit_extender_12
  assign cmn_o_out = bit_extender_12_out & ~{{2{not_20_out[3]}}, not_20_out[1], not_20_out[3]};  // AND_Gate cmn_o, 4 bits wide
  not not_20 (not_20_out[1], not_20_out[3]);
  assign bit_extender_13_out = {{3{not_22_out[2]}}, not_22_out[2]};  // Bit_Extender bit_extender_13
  assign orr_o_out = bit_extender_13_out & ~{not_22_out, not_22_out[2]};  // AND_Gate orr_o, 4 bits wide
  not not_21 (not_22_out[3], not_22_out[2]);
  not not_22 (not_22_out[1], not_22_out[2]);
  assign bit_extender_14_out = {{3{not_23_out[3]}}, not_23_out[3]};  // Bit_Extender bit_extender_14
  assign mov_o_out = bit_extender_14_out & ~{{2{not_23_out[3]}}, not_23_out[1], not_23_out[3]};  // AND_Gate mov_o, 4 bits wide
  not not_23 (not_23_out[1], not_23_out[3]);
  assign bit_extender_15_out = {{3{decoder_1_out14[2]}}, decoder_1_out14[2]};  // Bit_Extender bit_extender_15
  assign bic_o_out = bit_extender_15_out & ~{decoder_1_out14, {2{decoder_1_out14[2]}}};  // AND_Gate bic_o, 4 bits wide
  not not_24 (decoder_1_out14[3], decoder_1_out14[2]);
  assign bit_extender_16_out = {{3{not_25_out[3]}}, not_25_out[3]};  // Bit_Extender bit_extender_16
  assign mvn_o_out = bit_extender_16_out & ~{{2{not_25_out[3]}}, not_25_out[1], not_25_out[3]};  // AND_Gate mvn_o, 4 bits wide
  not not_25 (not_25_out[1], not_25_out[3]);
  assign ALU_op = and_o_out | eor_o_out | sub_o_out | rsb_o_out | add_o_out | adc_o_out | sbc_o_out | rsc_o_out | tst_o_out | teq_o_out | cmp_o_out | cmn_o_out | orr_o_out | mov_o_out | bic_o_out | mvn_o_out;  // OR_Gate or_6, 4 bits wide

  assign S = SCF;

  // Notes on the sheet:
  //   Need move ops to be 0
endmodule

module MEMdecode (
  input  [4:0] OpCode,
  output PostAddr,
  output OffAddr,
  output PreAddr,
  output Norm,
  output [3:0] ALUOp,
  output [1:0] MEMOp
);

  wire [3:0] Add_out, bit_extender_1_out, bit_extender_2_out, Sub_out;
  wire [3:1] not_2_out, not_3_out;

  and and_1 (PostAddr, ~OpCode[0], OpCode[3]);  // AND_Gate
  and and_2 (OffAddr, OpCode[0], ~OpCode[3]);  // AND_Gate
  and and_3 (PreAddr, OpCode[0], OpCode[3]);
  Decoder #(.enable("false")) decoder_1 (.out0(not_2_out[3]), .out1(not_3_out[3]), .sel(OpCode[1]));
  assign bit_extender_1_out = {{3{not_2_out[3]}}, not_2_out[3]};  // Bit_Extender bit_extender_1
  assign Sub_out = bit_extender_1_out & ~{not_2_out, not_2_out[3]};  // AND_Gate Sub, 4 bits wide
  not not_1 (not_2_out[2], not_2_out[3]);
  not not_2 (not_2_out[1], not_2_out[3]);
  assign bit_extender_2_out = {{3{not_3_out[3]}}, not_3_out[3]};  // Bit_Extender bit_extender_2
  assign Add_out = bit_extender_2_out & ~{{2{not_3_out[3]}}, not_3_out[1], not_3_out[3]};  // AND_Gate Add, 4 bits wide
  not not_3 (not_3_out[1], not_3_out[3]);
  and and_4 (Norm, ~PostAddr, ~OffAddr, ~PreAddr);  // AND_Gate
  assign ALUOp = Sub_out | Add_out;  // OR_Gate or_1, 4 bits wide

  assign MEMOp = {OpCode[4], OpCode[2]};

  // Other names for the same wires on the sheet: B = OpCode[2]; L = OpCode[4]; P = OpCode[0]; U = OpCode[1];
  //   W = OpCode[3]

  // Notes on the sheet:
  //   11 -> pre-index addressing
  //   00 -> Normal Operations
  //   01 -> translation stores
  //   10 -> offset addressing
  //   00 -> SW
  //   01 -> SBU
  //   10 -> LW
  //   11 -> LBU
endmodule

module BRAdecode (
  input  [3:0] Cond,
  input  LorH,
  input  One,
  input  [23:0] Baddr,
  input  [31:0] PC,
  output Link,
  output [31:0] MAddr
);

  wire and_1_out;
  wire [31:0] PC_t;

  and and_1 (and_1_out, Cond[0], Cond[1], Cond[2], Cond[3]);
  PCincr pcincr_1 (.PC(PC), .PC4(PC_t));
  not not_1 (MAddr[0], One);
  assign MAddr[31:2] = {{6{Baddr[23]}}, Baddr};  // Bit_Extender bit_extender_1
  Multiplexer #(.enable("false")) multiplexer_1 (.in0(MAddr[0]), .in1(LorH), .out(MAddr[1]), .sel(and_1_out));
  and and_2 (Link, LorH, ~and_1_out);  // AND_Gate
  Adder #(.width(32)) adder_1 (.a(PC_t));  // open: b, out, cin, cout

  // Notes on the sheet:
  //   still need to change cpsr
  //   if 1 then blx
  //   Calculating Branches in Decode
  //   0 if B, 1 if BL
endmodule

module OP2decode (
  input  [31:0] Inst,
  output IsLd,
  output [4:0] SRimm,
  output [31:0] Imm,
  output Rot,
  output [1:0] SOp,
  output Shift,
  output [3:0] Rm,
  output [3:0] Rs,
  output SrSi
);

  wire and_1_out, and_3_out, and_4_out, and_5_out, and_10_out;
  wire [0:0] not_1_out;
  wire [1:0] and_6_out, and_7_out, bit_extender_1_out, bit_extender_2_out;
  wire [4:0] and_9_out, bit_extender_3_out;

  and and_1 (and_1_out, ~Inst[27], ~Inst[26], Inst[25]);  // AND_Gate
  and and_2 (Rot, and_1_out, ~and_3_out);  // AND_Gate
  and and_3 (and_3_out, ~Inst[27], ~Inst[26], Inst[25], Inst[24], ~Inst[22], ~Inst[21], ~Inst[20]);  // AND_Gate
  and and_4 (and_4_out, ~Inst[27], ~Inst[26], ~Inst[25]);  // AND_Gate
  and and_5 (and_5_out, ~Inst[27], Inst[26], Inst[25]);  // AND_Gate
  assign bit_extender_1_out = {{1{Rot}}, Rot};  // Bit_Extender bit_extender_1
  assign bit_extender_2_out = {{1{Shift}}, Shift};  // Bit_Extender bit_extender_2
  or or_1 (Shift, and_4_out, and_5_out);
  assign and_6_out = bit_extender_1_out & {2{Rot}};  // AND_Gate and_6, 2 bits wide
  assign and_7_out = Inst[6:5] & bit_extender_2_out;  // AND_Gate and_7, 2 bits wide
  and and_8 (IsLd, Inst[27], ~Inst[26]);  // AND_Gate
  not not_1 (not_1_out[0], Rot);
  assign SOp = and_6_out | and_7_out;  // OR_Gate or_2, 2 bits wide
  assign bit_extender_3_out = {{4{Shift}}, Shift};  // Bit_Extender bit_extender_3
  assign Imm = {{24{1'b0}}, Inst[7:0]};  // Bit_Extender bit_extender_4
  assign and_9_out = {Inst[11:8], not_1_out[0]} & bit_extender_3_out;  // AND_Gate and_9, 5 bits wide
  Multiplexer #(.width(5), .enable("false")) multiplexer_1 (
    .in0(Inst[11:7]), .in1(and_9_out), .out(SRimm), .sel(and_10_out));
  and and_10 (and_10_out, Rot, Shift);

  assign Rm = Inst[3:0];
  assign Rs = Inst[11:8];
  assign SrSi = Inst[4];

  // Other names for the same wires on the sheet: C[3:0] = Inst[31:28]; F[1:0] = Inst[27:26]; S = Inst[20];
  //   I = Inst[25]; O[3:0] = Inst[24:21]; Imm8[7:0] = Inst[7:0]; OP2[11:0] = Inst[11:0]; SRorSI = Inst[4];
  //   SOp_t[1:0] = Inst[6:5]; SI[4:0] = Inst[11:7]; RotImm[3:0] = Inst[11:8]; Rd[3:0] = Inst[15:12];
  //   Rn[3:0] = Inst[19:16]

  // Notes on the sheet:
  //   1 if register shift and 0 if shift immediate
  //   This includes rotates and shift imms
endmodule

module CPSRDecode (
  input  [31:0] Cspr,
  input  [3:0] Cond,
  output Execute
);

  wire AL, and_1_out, and_2_out, and_3_out, and_4_out, and_5_out, and_6_out, and_7_out, and_8_out, and_9_out,
       and_10_out, and_11_out, and_12_out, and_13_out, and_14_out, EQ, GE, GT, HI, HS, LE, LO, LS, LT, MI,
       NE, NV, or_1_out, or_2_out, or_3_out, or_4_out, or_5_out, or_6_out, or_7_out, or_8_out, or_9_out,
       or_10_out, or_11_out, or_12_out, or_13_out, PL, VC, VS;

  Decoder #(.select(4), .enable("false")) decoder_1 (
    .out0(EQ), .out1(NE), .out2(HS), .out3(LO), .out4(MI), .out5(PL), .out6(VS), .out7(VC), .out8(HI),
    .out9(LS), .out10(GE), .out11(LT), .out12(GT), .out13(LE), .out14(AL), .out15(NV), .sel(Cond));
  and and_1 (and_1_out, EQ, Cspr[30]);
  and and_2 (and_2_out, NE, ~Cspr[30]);  // AND_Gate
  and and_3 (and_3_out, HS, Cspr[29]);
  and and_4 (and_4_out, LO, ~Cspr[29]);  // AND_Gate
  and and_5 (and_5_out, MI, Cspr[31]);
  and and_6 (and_6_out, PL, ~Cspr[31]);  // AND_Gate
  and and_7 (and_7_out, VS, Cspr[28]);
  and and_8 (and_8_out, VC, ~Cspr[28]);  // AND_Gate
  and and_9 (and_9_out, HI, Cspr[29], ~Cspr[30]);  // AND_Gate
  or or_1 (or_1_out, ~Cspr[29], Cspr[30]);  // OR_Gate
  or or_2 (or_2_out, Cspr[28], Cspr[31]);
  or or_3 (or_3_out, ~Cspr[28], ~Cspr[31]);  // OR_Gate
  or or_4 (or_4_out, ~Cspr[28], Cspr[31]);  // OR_Gate
  or or_5 (or_5_out, Cspr[28], ~Cspr[31]);  // OR_Gate
  or or_6 (or_6_out, Cspr[28], ~Cspr[30], Cspr[31]);  // OR_Gate
  or or_7 (or_7_out, ~Cspr[28], ~Cspr[30], ~Cspr[31]);  // OR_Gate
  or or_8 (or_8_out, ~Cspr[28], Cspr[30], Cspr[31]);  // OR_Gate
  or or_9 (or_9_out, Cspr[28], Cspr[30], ~Cspr[31]);  // OR_Gate
  and and_10 (and_10_out, or_1_out, LS);
  or or_10 (or_10_out, or_2_out, or_3_out);
  or or_11 (or_11_out, or_4_out, or_5_out);
  or or_12 (or_12_out, or_6_out, or_7_out);
  or or_13 (or_13_out, or_8_out, or_9_out);
  and and_11 (and_11_out, or_10_out, GE);
  and and_12 (and_12_out, or_11_out, LT);
  and and_13 (and_13_out, or_12_out, GT);
  and and_14 (and_14_out, or_13_out, LE);
  or or_14 (Execute, and_1_out, and_2_out, and_3_out, and_4_out, and_5_out, and_6_out, and_7_out, and_8_out, and_9_out, and_10_out, and_11_out, and_12_out, and_13_out, and_14_out, AL);

  // Other names for the same wires on the sheet: b0 = Cspr[28]; b1 = Cspr[29]; b2 = Cspr[30]; b3 = Cspr[31]
endmodule

module RegFile (
  input  [31:0] cpsrIn,
  input  S,
  input  [31:0] W,
  input  WE,
  input  Clk,
  input  [3:0] rM,
  input  [3:0] rW,
  input  [3:0] rN,
  input  [3:0] rS,
  output [31:0] cpsrOut,
  output [31:0] M,
  output [31:0] N,
  output [31:0] SV
);

  wire and_1_out, and_2_out, and_3_out, and_4_out, and_5_out, and_6_out, and_7_out, and_8_out, and_9_out,
       and_10_out, and_11_out, and_12_out, and_13_out, and_14_out, and_15_out, and_16_out, r0, r1, r2, r3,
       r4, r5, r6, r7, r8, r9, r10, r11, r12, r13, r14, r15;
  wire [31:0] a1, a2, a3, a4, ip, lr, pc, sp, v1, v2, v3, v4, v5, v6, v7, v8;

  Decoder #(.select(4), .enable("false")) decoder_1 (
    .out0(r0), .out1(r1), .out2(r2), .out3(r3), .out4(r4), .out5(r5), .out6(r6), .out7(r7), .out8(r8),
    .out9(r9), .out10(r10), .out11(r11), .out12(r12), .out13(r13), .out14(r14), .out15(r15), .sel(rW));
  Register #(.width(32), .trigger("falling")) cpsr (.D(cpsrIn), .en(S), .clk(Clk), .Q(cpsrOut));  // open: clr
  Register #(.width(32), .trigger("falling")) u_a1 (.D(W), .en(and_1_out), .clk(Clk), .Q(a1));  // open: clr
  and and_1 (and_1_out, WE, r0);
  Register #(.width(32), .trigger("falling")) u_a2 (.D(W), .en(and_2_out), .clk(Clk), .Q(a2));  // open: clr
  and and_2 (and_2_out, WE, r1);
  Register #(.width(32), .trigger("falling")) u_a3 (.D(W), .en(and_3_out), .clk(Clk), .Q(a3));  // open: clr
  and and_3 (and_3_out, WE, r2);
  Register #(.width(32), .trigger("falling")) u_a4 (.D(W), .en(and_4_out), .clk(Clk), .Q(a4));  // open: clr
  and and_4 (and_4_out, WE, r3);
  Register #(.width(32), .trigger("falling")) u_v1 (.D(W), .en(and_5_out), .clk(Clk), .Q(v1));  // open: clr
  and and_5 (and_5_out, WE, r4);
  Register #(.width(32), .trigger("falling")) u_v2 (.D(W), .en(and_6_out), .clk(Clk), .Q(v2));  // open: clr
  and and_6 (and_6_out, WE, r5);
  Register #(.width(32), .trigger("falling")) u_v3 (.D(W), .en(and_7_out), .clk(Clk), .Q(v3));  // open: clr
  and and_7 (and_7_out, WE, r6);
  Register #(.width(32), .trigger("falling")) u_v4 (.D(W), .en(and_8_out), .clk(Clk), .Q(v4));  // open: clr
  and and_8 (and_8_out, WE, r7);
  Register #(.width(32), .trigger("falling")) u_v5 (.D(W), .en(and_9_out), .clk(Clk), .Q(v5));  // open: clr
  and and_9 (and_9_out, WE, r8);
  Register #(.width(32), .trigger("falling")) u_v6 (.D(W), .en(and_10_out), .clk(Clk), .Q(v6));  // open: clr
  and and_10 (and_10_out, WE, r9);
  Register #(.width(32), .trigger("falling")) u_v7 (.D(W), .en(and_11_out), .clk(Clk), .Q(v7));  // open: clr
  and and_11 (and_11_out, WE, r10);
  Register #(.width(32), .trigger("falling")) u_v8 (.D(W), .en(and_12_out), .clk(Clk), .Q(v8));  // open: clr
  and and_12 (and_12_out, WE, r11);
  Register #(.width(32), .trigger("falling")) u_ip (.D(W), .en(and_13_out), .clk(Clk), .Q(ip));  // open: clr
  and and_13 (and_13_out, WE, r12);
  Register #(.width(32), .trigger("falling")) u_sp (.D(W), .en(and_14_out), .clk(Clk), .Q(sp));  // open: clr
  and and_14 (and_14_out, WE, r13);
  Register #(.width(32), .trigger("falling")) u_lr (.D(W), .en(and_15_out), .clk(Clk), .Q(lr));  // open: clr
  and and_15 (and_15_out, WE, r14);
  Register #(.width(32), .trigger("falling")) register_1 (.D(W), .en(and_16_out), .clk(Clk), .Q(pc));  // open: clr
  and and_16 (and_16_out, WE, r15);
  Multiplexer #(.select(4), .width(32), .enable("false")) multiplexer_1 (
    .in0(a1), .in1(a2), .in2(a3), .in3(a4), .in4(v1), .in5(v2), .in6(v3), .in7(v4), .in8(v5), .in9(v6),
    .in10(v7), .in11(v8), .in12(ip), .in13(sp), .in14(lr), .in15(pc), .out(M), .sel(rM));
  Multiplexer #(.select(4), .width(32), .enable("false")) multiplexer_2 (
    .in0(a1), .in1(a2), .in2(a3), .in3(a4), .in4(v1), .in5(v2), .in6(v3), .in7(v4), .in8(v5), .in9(v6),
    .in10(v7), .in11(v8), .in12(ip), .in13(sp), .in14(lr), .in15(pc), .out(N), .sel(rN));
  Multiplexer #(.select(4), .width(32), .enable("false")) multiplexer_3 (
    .in0(a1), .in1(a2), .in2(a3), .in3(a4), .in4(v1), .in5(v2), .in6(v3), .in7(v4), .in8(v5), .in9(v6),
    .in10(v7), .in11(v8), .in12(ip), .in13(sp), .in14(lr), .in15(pc), .out(SV), .sel(rS));
endmodule

module DE (
  input  [31:0] M,
  input  [31:0] N,
  input  [31:0] S,
  input  [31:0] In_Imm,
  input  [31:0] In_Addr,
  input  In_BL,
  input  [5:0] In_Shift,
  input  [31:0] In_CPSR,
  input  [6:0] In_ALU,
  input  [3:0] Rd,
  input  [5:0] In_Mem,
  input  [5:0] In_Flags,
  input  [4:0] In_SRI,
  input  [11:0] In_Reg,
  input  St,
  input  WE,
  input  CLK,
  output [31:0] Mo,
  output [31:0] No,
  output [31:0] So,
  output [31:0] Out_Imm,
  output [31:0] Out_Addr,
  output Out_BL,
  output [5:0] Out_Shift,
  output [31:0] Out_CPSR,
  output [6:0] Out_ALU,
  output [3:0] Rdo,
  output [5:0] Out_Mem,
  output [5:0] Out_Flags,
  output [4:0] Out_SRI,
  output [11:0] Out_Reg
);

  wire and_9_out;
  wire [3:0] and_7_out, bit_extender_3_out;
  wire [4:0] and_11_out, bit_extender_6_out;
  wire [5:0] and_8_out, and_10_out, and_13_out, bit_extender_4_out, bit_extender_5_out, bit_extender_12_out;
  wire [6:0] and_6_out, bit_extender_2_out;
  wire [11:0] and_12_out, bit_extender_7_out;
  wire [31:0] and_1_out, and_2_out, and_3_out, and_4_out, and_5_out, and_14_out, bit_extender_1_out,
       bit_extender_8_out, bit_extender_9_out, bit_extender_10_out, bit_extender_11_out, bit_extender_13_out;

  assign bit_extender_1_out = {{31{St}}, St};  // Bit_Extender bit_extender_1
  assign bit_extender_2_out = {{6{St}}, St};  // Bit_Extender bit_extender_2
  assign bit_extender_3_out = {{3{St}}, St};  // Bit_Extender bit_extender_3
  assign bit_extender_4_out = {{5{St}}, St};  // Bit_Extender bit_extender_4
  assign bit_extender_5_out = {{5{St}}, St};  // Bit_Extender bit_extender_5
  assign bit_extender_6_out = {{4{St}}, St};  // Bit_Extender bit_extender_6
  assign bit_extender_7_out = {{11{St}}, St};  // Bit_Extender bit_extender_7
  assign and_1_out = M & bit_extender_1_out;  // AND_Gate and_1, 32 bits wide
  assign and_2_out = N & bit_extender_8_out;  // AND_Gate and_2, 32 bits wide
  assign bit_extender_8_out = {{31{St}}, St};  // Bit_Extender bit_extender_8
  assign and_3_out = S & bit_extender_9_out;  // AND_Gate and_3, 32 bits wide
  assign bit_extender_9_out = {{31{St}}, St};  // Bit_Extender bit_extender_9
  assign and_4_out = In_Imm & bit_extender_10_out;  // AND_Gate and_4, 32 bits wide
  assign bit_extender_10_out = {{31{St}}, St};  // Bit_Extender bit_extender_10
  assign and_5_out = In_Addr & bit_extender_11_out;  // AND_Gate and_5, 32 bits wide
  assign bit_extender_11_out = {{31{St}}, St};  // Bit_Extender bit_extender_11
  assign bit_extender_12_out = {{5{St}}, St};  // Bit_Extender bit_extender_12
  assign bit_extender_13_out = {{31{St}}, St};  // Bit_Extender bit_extender_13
  assign and_6_out = In_ALU & bit_extender_2_out;  // AND_Gate and_6, 7 bits wide
  assign and_7_out = Rd & bit_extender_3_out;  // AND_Gate and_7, 4 bits wide
  assign and_8_out = In_Mem & bit_extender_4_out;  // AND_Gate and_8, 6 bits wide
  and and_9 (and_9_out, In_BL, St);
  assign and_10_out = In_Flags & bit_extender_5_out;  // AND_Gate and_10, 6 bits wide
  assign and_11_out = In_SRI & bit_extender_6_out;  // AND_Gate and_11, 5 bits wide
  assign and_12_out = In_Reg & bit_extender_7_out;  // AND_Gate and_12, 12 bits wide
  Register #(.width(32)) register_1 (.D(and_1_out), .en(WE), .clk(CLK), .Q(Mo));  // open: clr
  Register #(.width(32)) register_2 (.D(and_2_out), .en(WE), .clk(CLK), .Q(No));  // open: clr
  Register #(.width(32)) register_3 (.D(and_4_out), .en(WE), .clk(CLK), .Q(Out_Imm));  // open: clr
  Register #(.width(32)) register_4 (.D(and_5_out), .en(WE), .clk(CLK), .Q(Out_Addr));  // open: clr
  Register #(.width(6)) register_5 (.D(and_13_out), .en(WE), .clk(CLK), .Q(Out_Shift));  // open: clr
  assign and_13_out = In_Shift & bit_extender_12_out;  // AND_Gate and_13, 6 bits wide
  assign and_14_out = In_CPSR & bit_extender_13_out;  // AND_Gate and_14, 32 bits wide
  Register #(.width(32)) register_6 (.D(and_14_out), .en(WE), .clk(CLK), .Q(Out_CPSR));  // open: clr
  Register #(.width(7)) register_7 (.D(and_6_out), .en(WE), .clk(CLK), .Q(Out_ALU));  // open: clr
  Register #(.width(4)) register_8 (.D(and_7_out), .en(WE), .clk(CLK), .Q(Rdo));  // open: clr
  Register #(.width(32)) register_9 (.D(and_3_out), .en(WE), .clk(CLK), .Q(So));  // open: clr
  Register #(.width(6)) register_10 (.D(and_8_out), .en(WE), .clk(CLK), .Q(Out_Mem));  // open: clr
  Register #(.width(1)) register_11 (.D(and_9_out), .en(WE), .clk(CLK), .Q(Out_BL));  // open: clr
  Register #(.width(6)) register_12 (.D(and_10_out), .en(WE), .clk(CLK), .Q(Out_Flags));  // open: clr
  Register #(.width(5)) register_13 (.D(and_11_out), .en(WE), .clk(CLK), .Q(Out_SRI));  // open: clr
  Register #(.width(12)) register_14 (.D(and_12_out), .en(WE), .clk(CLK), .Q(Out_Reg));  // open: clr

  // Notes on the sheet:
  //   0 extend the immediate
  //   shift?, rotate?, shift op?, Imm, shift reg
  //   ex, f, aluop
endmodule

module Execute (
  input  [31:0] N,
  input  [31:0] MemN,
  input  [31:0] WbN,
  input  [31:0] M,
  input  [31:0] MemM,
  input  [31:0] WbM,
  input  [1:0] ForwardN,
  input  [1:0] ForwardM,
  input  [1:0] ForwardS,
  input  [6:0] In_ALU,
  input  [4:0] In_SRI,
  input  [5:0] In_Shift,
  input  [5:0] In_Flags,
  input  [5:0] In_Mem,
  input  [3:0] In_Rd,
  input  [31:0] In_CPSR,
  input  [31:0] In_Imm,
  input  [31:0] In_Addr,
  input  [31:0] S,
  input  [4:0] MemS,
  input  [4:0] WbS,
  input  [11:0] In_Reg,
  input  BL,
  output [31:0] C,
  output [31:0] Out_CPSR,
  output [31:0] Out_Addr,
  output [3:0] Out_Rd,
  output [11:0] Out_Reg,
  output [31:0] Out_Data
);

  wire and_3_out, and_4_out, and_6_out, or_1_out;
  wire [3:0] COND_CALC;
  wire [4:0] and_1_out, bit_extender_1_out, multiplexer_2_out, mux3x1_5_1_so;
  wire [31:0] and_2_out, and_5_out, bit_extender_2_out, bit_extender_3_out, M_t, multiplexer_1_out,
       multiplexer_4_out, multiplexer_5_out, N_t, not_1_out, not_2_out, not_3_out, not_4_out, undriven;

  assign and_1_out = In_SRI & bit_extender_1_out;  // AND_Gate and_1, 5 bits wide
  assign bit_extender_1_out = {{4{In_Shift[0]}}, In_Shift[0]};  // Bit_Extender bit_extender_1
  Mux3x1_32 mux3x1_32_1 (.SWBEX(ForwardN[1]), .MW_I(WbN), .I(N), .EM_I(MemN), .SMEX(ForwardN[0]), .Io(N_t));
  Mux3x1_32 mux3x1_32_2 (.SWBEX(ForwardM[1]), .MW_I(WbM), .I(M), .EM_I(MemM), .SMEX(ForwardM[0]), .Io(M_t));
  Mux3x1_5 mux3x1_5_1 (
    .S(S[4:0]), .EM_S(MemS), .MW_S(WbS), .SMEX(ForwardS[0]), .SWBEX(ForwardS[1]), .So(mux3x1_5_1_so));
  assign bit_extender_2_out = {{31{In_Flags[0]}}, In_Flags[0]};  // Bit_Extender bit_extender_2
  assign not_1_out = ~bit_extender_2_out;  // NOT_Gate not_1, 32 bits wide
  assign and_2_out = not_1_out & N_t;  // AND_Gate and_2, 32 bits wide
  Multiplexer #(.width(32), .enable("false")) multiplexer_1 (
    .in0(M_t), .in1(In_Imm), .out(multiplexer_1_out), .sel(In_Shift[4]));
  Multiplexer #(.width(5), .enable("false")) multiplexer_2 (
    .in0(and_1_out), .in1(mux3x1_5_1_so), .out(multiplexer_2_out), .sel(and_3_out));
  and and_3 (and_3_out, ~and_4_out, In_Shift[5]);  // AND_Gate
  and and_4 (and_4_out, In_Shift[4], In_Flags[0]);
  // ARM_ALU arm_alu_1: pin names not known; wires that end beside it: multiplexer_1_out, In_Flags[3], In_ALU[3:0], multiplexer_2_out, In_Shift[3:2], COND_CALC
  Multiplexer #(.width(32), .enable("false")) multiplexer_3 (
    .in0(and_2_out), .in1(not_2_out), .sel(In_Flags[5]));  // open: out
  assign not_2_out = ~and_2_out;  // NOT_Gate not_2, 32 bits wide
  or or_1 (or_1_out, In_Flags[1], In_Flags[4]);
  Multiplexer #(.width(32), .enable("false")) multiplexer_4 (
    .in0(undriven), .in1(not_3_out), .out(multiplexer_4_out), .sel(In_Flags[5]));
  assign not_3_out = ~undriven;  // NOT_Gate not_3, 32 bits wide
  assign bit_extender_3_out = {{31{In_ALU[6]}}, In_ALU[6]};  // Bit_Extender bit_extender_3
  CPSRset cpsrset_1 (.CPSR(In_CPSR), .Ex(In_ALU[6]), .SCF(or_1_out), .COND(COND_CALC), .CPSRn(Out_CPSR));
  Multiplexer #(.width(32), .enable("false")) multiplexer_5 (
    .in0(and_5_out), .in1(not_4_out), .out(multiplexer_5_out), .sel(and_6_out));
  assign not_4_out = ~and_5_out;  // NOT_Gate not_4, 32 bits wide
  assign and_5_out = bit_extender_3_out & multiplexer_4_out;  // AND_Gate and_5, 32 bits wide
  and and_6 (and_6_out, In_Flags[0], In_ALU[3], In_ALU[2], In_ALU[1], In_ALU[0]);
  Multiplexer #(.width(32), .enable("false")) multiplexer_6 (.in0(multiplexer_5_out), .in1(In_Addr), .out(C), .sel(BL));

  assign Out_Addr = In_Addr;
  assign Out_Data = S;
  assign Out_Rd = In_Rd;
  assign Out_Reg = In_Reg;

  // Other names for the same wires on the sheet: BLink = BL; Imm[31:0] = In_Imm; F[1:0] = In_ALU[5:4]; Ex = In_ALU[6];
  //   mov = In_Flags[0]; cmp = In_Flags[1]; car = In_Flags[2]; rev = In_Flags[3]; SCF = In_Flags[4];
  //   Neg = In_Flags[5]; ToAddr[3:0] = In_Mem[3:0]; MEMOp[1:0] = In_Mem[5:4]; Shift = In_Shift[0]; Rot = In_Shift[1];
  //   SOp[1:0] = In_Shift[3:2]; I = In_Shift[4]; SrSi = In_Shift[5]

  // Notes on the sheet:
  //   ex, f, aluop
  //   shift?, rotate?, shift op?, Imm, shift reg
  //   mov, cmp, car, rev, scf
  //   Rn, Rm, Rs
  //   These operations have no Rn input
  //   reverse bit based on rev
  //   RM or an immediate
  //   Rs Forwarding
  //   Basically same thing
  //   If SrSi == 1 then send forwarded Rs value
  //   checks if MVN inst
endmodule

module CPSRset (
  input  [31:0] CPSR,
  input  Ex,
  input  SCF,
  input  [3:0] COND,
  output [31:0] CPSRn
);

  wire and_1_out;

  and and_1 (and_1_out, Ex, SCF);
  Multiplexer #(.width(32), .enable("false")) multiplexer_1 (
    .in0(CPSR), .in1({COND, CPSR[27:0]}), .out(CPSRn), .sel(and_1_out));

  // Other names for the same wires on the sheet: V = CPSR[28]; Z = CPSR[30]
endmodule

module BranchStall (
  input  [6:0] ALU_De,
  input  [31:0] In_Addr,
  input  [31:0] PC,
  input  In_BL,
  input  [5:0] MEM,
  input  [3:0] Rn,
  input  [3:0] Rm,
  input  [3:0] Rd,
  input  [6:0] ALU_Ex,
  output Branch,
  output [31:0] Out_addr,
  output Zap,
  output Stall
);

  wire and_2_out, and_3_out, and_4_out, eq_1_eq, eq_2_eq, or_1_out;

  and and_1 (Branch, ~ALU_De[4], ALU_De[5], ALU_De[6]);  // AND_Gate
  EQ eq_1 (.A(Rn), .B(Rd), .EQ(eq_1_eq));
  EQ eq_2 (.A(Rm), .B(Rd), .EQ(eq_2_eq));
  and and_2 (and_2_out, ALU_Ex[4], ~ALU_Ex[5]);  // AND_Gate
  or or_1 (or_1_out, eq_1_eq, eq_2_eq);
  and and_3 (and_3_out, MEM[5], and_2_out);
  and and_4 (and_4_out, and_3_out, or_1_out);
  not not_1 (Stall, and_4_out);

  assign Out_addr = In_Addr;
  assign Zap = Branch;

  // Notes on the sheet:
  //   Branch Link
  //   some other logic
endmodule

module Hazard (
  input  [3:0] M_Ex_D,
  input  [3:0] W_Ex_D,
  input  [11:0] In_ExecuteR,
  input  [5:0] In_Shift,
  input  [6:0] EnblM,
  input  [6:0] EnblW,
  output [1:0] ForwardN,
  output [1:0] ForwardM,
  output [1:0] ForwardS
);

  wire and_7_out, and_8_out, and_11_out, and_12_out, and_13_out, and_16_out, and_17_out, BranchM, BranchW,
       eq_1_eq, eq_2_eq, eq_3_eq, eq_4_eq, eq_5_eq, eq_6_eq, or_1_out, or_2_out;
  wire [1:0] and_3_out, and_5_out, and_6_out, and_14_out, and_15_out, bit_extender_1_out, bit_extender_2_out,
       bit_extender_3_out, bit_extender_4_out, bit_extender_5_out;

  EQ eq_1 (.A(M_Ex_D), .B(In_ExecuteR[11:8]), .EQ(eq_1_eq));
  EQ eq_2 (.A(M_Ex_D), .B(In_ExecuteR[7:4]), .EQ(eq_2_eq));
  EQ eq_3 (.A(M_Ex_D), .B(In_ExecuteR[3:0]), .EQ(eq_3_eq));
  EQ eq_4 (.A(W_Ex_D), .B(In_ExecuteR[11:8]), .EQ(eq_4_eq));
  EQ eq_5 (.A(W_Ex_D), .B(In_ExecuteR[7:4]), .EQ(eq_5_eq));
  EQ eq_6 (.A(W_Ex_D), .B(In_ExecuteR[3:0]), .EQ(eq_6_eq));
  and and_1 (BranchM, ~EnblM[4], EnblM[5]);  // AND_Gate
  and and_2 (BranchW, ~EnblW[4], EnblW[5]);  // AND_Gate
  and and_3 (and_3_out[0], EnblM[6], eq_1_eq);
  and and_4 (and_3_out[1], ~and_3_out[0], and_7_out);  // AND_Gate
  and and_5 (and_5_out[0], EnblM[6], eq_2_eq);
  and and_6 (and_6_out[0], EnblM[6], eq_3_eq);
  and and_7 (and_7_out, EnblW[6], eq_4_eq);
  and and_8 (and_8_out, EnblW[6], eq_5_eq);
  and and_9 (and_5_out[1], ~and_5_out[0], and_8_out);  // AND_Gate
  and and_10 (and_6_out[1], ~and_6_out[0], and_11_out);  // AND_Gate
  and and_11 (and_11_out, EnblW[6], eq_6_eq);
  assign bit_extender_1_out = {{1{In_Shift[1]}}, In_Shift[1]};  // Bit_Extender bit_extender_1
  assign bit_extender_2_out = {{1{In_Shift[1]}}, In_Shift[1]};  // Bit_Extender bit_extender_2
  and and_12 (and_12_out, and_3_out[0], ~and_3_out[1], BranchM);  // AND_Gate
  and and_13 (and_13_out, ~and_3_out[0], and_3_out[1], BranchW);  // AND_Gate
  assign and_14_out = and_5_out & ~bit_extender_1_out;  // AND_Gate and_14, 2 bits wide
  assign and_15_out = and_6_out & ~bit_extender_2_out;  // AND_Gate and_15, 2 bits wide
  assign bit_extender_3_out = {{1{In_Shift[0]}}, In_Shift[0]};  // Bit_Extender bit_extender_3
  or or_1 (or_1_out, and_12_out, and_13_out);
  and and_16 (and_16_out, and_14_out[0], ~and_14_out[1], BranchM);  // AND_Gate
  and and_17 (and_17_out, ~and_14_out[0], and_14_out[1], BranchW);  // AND_Gate
  assign ForwardS = and_15_out & ~bit_extender_3_out;  // AND_Gate and_18, 2 bits wide
  assign ForwardN = and_3_out & ~bit_extender_4_out;  // AND_Gate and_19, 2 bits wide
  assign bit_extender_4_out = {{1{or_1_out}}, or_1_out};  // Bit_Extender bit_extender_4
  or or_2 (or_2_out, and_16_out, and_17_out);
  assign ForwardM = and_14_out & ~bit_extender_5_out;  // AND_Gate and_20, 2 bits wide
  assign bit_extender_5_out = {{1{or_2_out}}, or_2_out};  // Bit_Extender bit_extender_5

  // Other names for the same wires on the sheet: enblM_t = EnblM[6]; enblW_t = EnblW[6]; Rs[3:0] = In_ExecuteR[3:0];
  //   Rm[3:0] = In_ExecuteR[7:4]; Rn[3:0] = In_ExecuteR[11:8]

  // Notes on the sheet:
  //   shift?, rotate?, shift op?, Imm, shift reg
  //   shift register bit on top, immediate bit on bottom
  //   01 m
  //   10 wb
endmodule

module EM (
  input  [31:0] In_Res,
  input  [31:0] In_Addr,
  input  [5:0] In_MemOp,
  input  [3:0] In_Rd,
  input  [6:0] In_AlLUOp,
  input  [11:0] In_Reg,
  input  [31:0] In_CPSR,
  input  [5:0] In_Flags,
  input  [31:0] In_Data,
  input  WE,
  input  CLK,
  output [31:0] Out_Res,
  output [31:0] Out_Addr,
  output [5:0] Out_MemOp,
  output [3:0] Out_Rd,
  output [6:0] Out_ALUOp,
  output [11:0] Out_Reg,
  output [31:0] Out_CPSR,
  output [5:0] Out_Flags,
  output [31:0] Out_Data
);

  Register #(.width(32)) register_1 (.D(In_Res), .en(WE), .clk(CLK), .Q(Out_Res));  // open: clr
  Register #(.width(32)) register_2 (.D(In_Addr), .en(WE), .clk(CLK), .Q(Out_Addr));  // open: clr
  Register #(.width(6)) register_3 (.D(In_MemOp), .en(WE), .clk(CLK), .Q(Out_MemOp));  // open: clr
  Register #(.width(4)) register_4 (.D(In_Rd), .en(WE), .clk(CLK), .Q(Out_Rd));  // open: clr
  Register #(.width(7)) register_5 (.D(In_AlLUOp), .en(WE), .clk(CLK), .Q(Out_ALUOp));  // open: clr
  Register #(.width(12)) register_6 (.D(In_Reg), .en(WE), .clk(CLK), .Q(Out_Reg));  // open: clr
  Register #(.width(32)) register_7 (.D(In_CPSR), .en(WE), .clk(CLK), .Q(Out_CPSR));  // open: clr
  Register #(.width(6)) register_8 (.D(In_Flags), .en(WE), .clk(CLK), .Q(Out_Flags));  // open: clr
  Register #(.width(32)) register_9 (.D(In_Data), .en(WE), .clk(CLK), .Q(Out_Data));  // open: clr
endmodule

module Memory (
  input  [31:0] In_Res,
  input  [31:0] In_Data,
  input  [5:0] In_MemOp,
  input  [6:0] In_ALUOp,
  input  [3:0] In_Rd,
  input  [31:0] In_CPSR,
  input  [5:0] In_Flags,
  input  CLK,
  output [31:0] Out_ResStore,
  output [3:0] Out_Rd,
  output [5:0] Out_Flags,
  output [31:0] Out_CPSR,
  output [6:0] out_ALUOp,
  output store,
  output Branch
);

  wire and_2_out, and_4_out, not_1_out, not_2_out, resS;
  wire [3:0] mips_ram_1_p3;
  wire [31:0] Data, DataSel, loadstore_1_mdata;

  and and_1 (resS, In_ALUOp[4], ~In_ALUOp[5], In_ALUOp[6]);  // AND_Gate
  and and_2 (and_2_out, In_ALUOp[4], ~In_ALUOp[5]);  // AND_Gate
  // AND_Gate and_3 has open pins: in0=and_2_out, in1=not_1_out, out=open
  and and_4 (and_4_out, and_2_out, In_MemOp[5]);
  not not_1 (not_1_out, In_MemOp[5]);
  // MIPS_RAM mips_ram_1: pin names not known; wires that end beside it: In_Res[21:2], Data, mips_ram_1_p3, CLK, and_4_out, DataSel
  LoadStore loadstore_1 (
    .ByteSel(In_Res[1:0]), .Data(In_Data), .WorB(In_MemOp[4]), .MDataIn(DataSel), .SelBy(mips_ram_1_p3),
    .DataOut(Data), .Mdata(loadstore_1_mdata));  // open: Sign
  and and_5 (Branch, ~In_ALUOp[4], In_ALUOp[5]);  // AND_Gate
  and and_6 (store, and_2_out, not_2_out);
  not not_2 (not_2_out, In_MemOp[5]);
  Multiplexer #(.width(32), .enable("false")) multiplexer_1 (
    .in0(In_Res), .in1(loadstore_1_mdata), .out(Out_ResStore), .sel(resS));

  assign out_ALUOp = In_ALUOp;
  assign Out_CPSR = In_CPSR;
  assign Out_Flags = In_Flags;
  assign Out_Rd = In_Rd;

  // Other names for the same wires on the sheet: str = In_MemOp[5]; BySel[1:0] = In_Res[1:0];
  //   toAddr[3:0] = In_MemOp[3:0]

  // Notes on the sheet:
  //   memop, toadd
  //   ex, for, aluop
endmodule

module LoadStore (
  input  [1:0] ByteSel,
  input  [31:0] Data,
  input  WorB,
  input  [31:0] MDataIn,
  input  Sign,
  output [3:0] SelBy,
  output [31:0] DataOut,
  output [31:0] Mdata
);

  wire [3:0] decoder_1_out0;
  wire [7:0] multiplexer_1_out;
  wire [31:0] bit_extender_1_out, bit_extender_2_out, multiplexer_4_out;

  Decoder #(.select(2), .enable("false")) decoder_1 (
    .out0(decoder_1_out0[0]), .out1(decoder_1_out0[1]), .out2(decoder_1_out0[2]), .out3(decoder_1_out0[3]),
    .sel(ByteSel));
  Multiplexer #(.select(2), .width(8), .enable("false")) multiplexer_1 (
    .in0(MDataIn[7:0]), .in1(MDataIn[15:8]), .in2(MDataIn[23:16]), .in3(MDataIn[31:24]),
    .out(multiplexer_1_out), .sel(ByteSel));
  assign bit_extender_1_out = {{24{1'b0}}, multiplexer_1_out};  // Bit_Extender bit_extender_1
  assign bit_extender_2_out = {{24{multiplexer_1_out[7]}}, multiplexer_1_out};  // Bit_Extender bit_extender_2
  Multiplexer #(.width(4), .enable("false")) multiplexer_2 (
    .in0(decoder_1_out0), .in1({4{WorB}}), .out(SelBy), .sel(WorB));
  Multiplexer #(.width(32), .enable("false")) multiplexer_3 (
    .in0({Data[7:0], Data[7:0], Data[7:0], Data[7:0]}), .in1(Data), .out(DataOut), .sel(WorB));
  Multiplexer #(.width(32), .enable("false")) multiplexer_4 (
    .in0(bit_extender_1_out), .in1(bit_extender_2_out), .out(multiplexer_4_out), .sel(Sign));
  Multiplexer #(.width(32), .enable("false")) multiplexer_5 (
    .in0(multiplexer_4_out), .in1(MDataIn), .out(Mdata), .sel(WorB));

  // Other names for the same wires on the sheet: Sel[1:0] = ByteSel

  // Notes on the sheet:
  //   0 if word, 1 if byte load/store
  //   for store byte or word
  //   for load bytes
endmodule

module MW (
  input  [31:0] In_Res,
  input  [3:0] In_Rd,
  input  [5:0] In_Flags,
  input  [11:0] In_Reg,
  input  [31:0] In_CPSR,
  input  [6:0] In_ALU,
  input  str,
  input  B,
  input  WE,
  input  CLK,
  output [31:0] Out_Res,
  output [3:0] Out_Rd,
  output [5:0] Out_Flags,
  output [31:0] Out_CPSR,
  output [11:0] Out_Reg,
  output [6:0] Out_ALU,
  output str_o,
  output B_o
);

  Register #(.width(32)) register_1 (.D(In_Res), .en(WE), .clk(CLK), .Q(Out_Res));  // open: clr
  Register #(.width(4)) register_2 (.D(In_Rd), .en(WE), .clk(CLK), .Q(Out_Rd));  // open: clr
  Register #(.width(6)) register_3 (.D(In_Flags), .en(WE), .clk(CLK), .Q(Out_Flags));  // open: clr
  Register #(.width(12)) register_4 (.D(In_Reg), .en(WE), .clk(CLK), .Q(Out_Reg));  // open: clr
  Register #(.width(32)) register_5 (.D(In_CPSR), .en(WE), .clk(CLK), .Q(Out_CPSR));  // open: clr
  Register #(.width(7)) register_6 (.D(In_ALU), .en(WE), .clk(CLK), .Q(Out_ALU));  // open: clr
  Register #(.width(1)) register_7 (.D(str), .en(WE), .clk(CLK), .Q(str_o));  // open: clr
  Register #(.width(1)) register_8 (.D(B), .en(WE), .clk(CLK), .Q(B_o));  // open: clr
endmodule

module Shift (
  input  [31:0] M,
  input  [4:0] S,
  input  [1:0] SOp,
  output [31:0] Mn
);

  wire and_1_out, and_2_out, multiplexer_1_out, or_1_out, or_2_out, xor_1_out;
  wire [31:0] ls_1_mn, multiplexer_2_out, switch_1_mn, switch_2_mn;

  xor xor_1 (xor_1_out, SOp[0], SOp[0]);
  Switch switch_1 (.M(M), .Mn(switch_1_mn));
  Multiplexer #(.enable("false")) multiplexer_1 (
    .in0(xor_1_out), .in1(M[31]), .out(multiplexer_1_out), .sel(and_1_out));
  and and_1 (and_1_out, ~SOp[0], SOp[1]);  // AND_Gate
  Multiplexer #(.width(32), .enable("false")) multiplexer_2 (
    .in0(M), .in1(switch_1_mn), .out(multiplexer_2_out), .sel(or_1_out));
  or or_1 (or_1_out, SOp[0], SOp[1]);
  and and_2 (and_2_out, SOp[0], SOp[1]);
  LS ls_1 (.M(multiplexer_2_out), .S(S), .C(multiplexer_1_out), .R(and_2_out), .Mn(ls_1_mn));
  Multiplexer #(.width(32), .enable("false")) multiplexer_3 (
    .in0(ls_1_mn), .in1(switch_2_mn), .out(Mn), .sel(or_2_out));
  Switch switch_2 (.M(ls_1_mn), .Mn(switch_2_mn));
  or or_2 (or_2_out, SOp[0], SOp[1]);
endmodule

module LS (
  input  [31:0] M,
  input  [4:0] S,
  input  C,
  input  R,
  output [31:0] Mn
);

  wire [31:0] l2_1_mn, l4_1_mn, l8_1_mn, l16_1_mn;

  L16 l16_1 (.M(M), .S(S[4]), .C(C), .R(R), .Mn(l16_1_mn));
  L8 l8_1 (.M(l16_1_mn), .S(S[3]), .C(C), .R(R), .Mn(l8_1_mn));
  L4 l4_1 (.M(l8_1_mn), .S(S[2]), .C(C), .R(R), .Mn(l4_1_mn));
  L2 l2_1 (.M(l4_1_mn), .S(S[1]), .C(C), .R(R), .Mn(l2_1_mn));
  L1 l1_1 (.M(l2_1_mn), .S(S[0]), .C(C), .R(R), .Mn(Mn));
endmodule

module L1 (
  input  [31:0] M,
  input  S,
  input  C,
  input  R,
  output [31:0] Mn
);

  wire [0:0] multiplexer_1_out;

  Multiplexer #(.enable("false")) multiplexer_1 (.in0(C), .in1(M[31]), .out(multiplexer_1_out[0]), .sel(R));
  Multiplexer #(.width(32), .enable("false")) multiplexer_2 (
    .in0(M), .in1({M[30:0], multiplexer_1_out[0]}), .out(Mn), .sel(S));
endmodule

module L2 (
  input  [31:0] M,
  input  S,
  input  C,
  input  R,
  output [31:0] Mn
);

  wire [1:0] bit_extender_1_out, multiplexer_1_out;

  assign bit_extender_1_out = {{1{C}}, C};  // Bit_Extender bit_extender_1
  Multiplexer #(.width(2), .enable("false")) multiplexer_1 (
    .in0(bit_extender_1_out), .in1({M[30], M[31]}), .out(multiplexer_1_out), .sel(R));
  Multiplexer #(.width(32), .enable("false")) multiplexer_2 (
    .in0(M), .in1({M[29:0], multiplexer_1_out[0], multiplexer_1_out[1]}), .out(Mn), .sel(S));
endmodule

module L4 (
  input  [31:0] M,
  input  S,
  input  C,
  input  R,
  output [31:0] Mn
);

  wire [3:0] bit_extender_1_out, multiplexer_1_out;

  assign bit_extender_1_out = {{3{C}}, C};  // Bit_Extender bit_extender_1
  Multiplexer #(.width(4), .enable("false")) multiplexer_1 (
    .in0(bit_extender_1_out), .in1({M[28], M[29], M[30], M[31]}), .out(multiplexer_1_out), .sel(R));
  Multiplexer #(.width(32), .enable("false")) multiplexer_2 (
    .in0(M),
    .in1({M[27:0], multiplexer_1_out[0], multiplexer_1_out[1], multiplexer_1_out[2], multiplexer_1_out[3]}),
    .out(Mn), .sel(S));
endmodule

module L8 (
  input  [31:0] M,
  input  S,
  input  C,
  input  R,
  output [31:0] Mn
);

  wire [7:0] bit_extender_1_out, multiplexer_1_out;

  assign bit_extender_1_out = {{7{C}}, C};  // Bit_Extender bit_extender_1
  Multiplexer #(.width(8), .enable("false")) multiplexer_1 (
    .in0(bit_extender_1_out), .in1({M[24], M[25], M[26], M[27], M[28], M[29], M[30], M[31]}),
    .out(multiplexer_1_out), .sel(R));
  Multiplexer #(.width(32), .enable("false")) multiplexer_2 (
    .in0(M),
    .in1({M[23:0], multiplexer_1_out[0], multiplexer_1_out[1], multiplexer_1_out[2], multiplexer_1_out[3], multiplexer_1_out[4], multiplexer_1_out[5], multiplexer_1_out[6], multiplexer_1_out[7]}),
    .out(Mn), .sel(S));
endmodule

module L16 (
  input  [31:0] M,
  input  S,
  input  C,
  input  R,
  output [31:0] Mn
);

  wire [15:0] bit_extender_1_out, multiplexer_1_out;

  assign bit_extender_1_out = {{15{C}}, C};  // Bit_Extender bit_extender_1
  Multiplexer #(.width(16), .enable("false")) multiplexer_1 (
    .in0(bit_extender_1_out),
    .in1({M[16], M[17], M[18], M[19], M[20], M[21], M[22], M[23], M[24], M[25], M[26], M[27], M[28], M[29], M[30], M[31]}),
    .out(multiplexer_1_out), .sel(R));
  Multiplexer #(.width(32), .enable("false")) multiplexer_2 (
    .in0(M),
    .in1({M[15:0], multiplexer_1_out[0], multiplexer_1_out[1], multiplexer_1_out[2], multiplexer_1_out[3], multiplexer_1_out[4], multiplexer_1_out[5], multiplexer_1_out[6], multiplexer_1_out[7], multiplexer_1_out[8], multiplexer_1_out[9], multiplexer_1_out[10], multiplexer_1_out[11], multiplexer_1_out[12], multiplexer_1_out[13], multiplexer_1_out[14], multiplexer_1_out[15]}),
    .out(Mn), .sel(S));
endmodule

module Switch (
  input  [31:0] M,
  output [31:0] Mn
);


  assign Mn = {M[0], M[1], M[2], M[3], M[4], M[5], M[6], M[7], M[8], M[9], M[10], M[11], M[12], M[13], M[14], M[15], M[16], M[17], M[18], M[19], M[20], M[21], M[22], M[23], M[24], M[25], M[26], M[27], M[28], M[29], M[30], M[31]};
endmodule

module Mux3x1_5 (
  input  [4:0] S,
  input  [4:0] EM_S,
  input  [4:0] MW_S,
  input  SMEX,
  input  SWBEX,
  output [4:0] So
);

  wire [4:0] multiplexer_1_out;

  Multiplexer #(.width(5), .enable("false")) multiplexer_1 (.in0(S), .in1(EM_S), .out(multiplexer_1_out), .sel(SMEX));
  Multiplexer #(.width(5), .enable("false")) multiplexer_2 (.in0(multiplexer_1_out), .in1(MW_S), .out(So), .sel(SWBEX));
endmodule

module Mux3x1_32 (
  input  [31:0] I,
  input  [31:0] EM_I,
  input  [31:0] MW_I,
  input  SMEX,
  input  SWBEX,
  output [31:0] Io
);

  wire [31:0] multiplexer_1_out;

  Multiplexer #(.width(32), .enable("false")) multiplexer_1 (.in0(I), .in1(EM_I), .out(multiplexer_1_out), .sel(SMEX));
  Multiplexer #(.width(32), .enable("false")) multiplexer_2 (
    .in0(multiplexer_1_out), .in1(MW_I), .out(Io), .sel(SWBEX));
endmodule

module EQ (
  input  [3:0] A,
  input  [3:0] B,
  output EQ
);

  wire [3:0] xnor_1_out;

  assign xnor_1_out = ~(A ^ B);  // XNOR_Gate xnor_1, 4 bits wide
  and and_1 (EQ, xnor_1_out[0], xnor_1_out[1], xnor_1_out[2], xnor_1_out[3]);
endmodule

module PCincr (
  input  [31:0] PC,
  output [31:0] PC4
);

  // Incrementer #(.width(30)) incrementer_1: pin names not known; wires that end beside it: PC[31:2], PC4[31:2]

  assign PC4[1:0] = PC[1:0];
endmodule
